// Digital circuit cpu-32 test.dig as structural Verilog
module cpu_32_test (
  input  E,
  input  [31:0] I_D__bus,
  input  [31:0] D_D__bus,
  input  [31:0] I_A__bus,
  input  [31:0] D_A__bus,
  input  INT_nor,
  input  INT_nmk,
  input  run,
  input  I_valid,
  input  D_accept,
  input  C,
  input  [31:0] INT_vec,
  input  B_used,
  output I_LD,
  output D_LD,
  output D_ST,
  output [1:0] MMU_sel,
  output MMU_str,
  output [2:0] DMA_sel,
  output DMA_str,
  output INT_str,
  output CLK_str,
  output [1:0] CSH_mode,
  output CSH_run,
  output INT_out,
  output [1:0] D_MD
);

  wire alu_32_1_p6, alu_32_1_p9, ALU_A_CLR, ALU_A_CMP, ALU_A_DRD, ALU_A_DRE, ALU_A_FRD, ALU_A_FRE, ALU_A_LD,
       ALU_A_LRD, ALU_A_STD, ALU_A_STF, ALU_A_UUD, ALU_A_UUF, ALU_A_V, ALU_A_VD, ALU_A_VF, ALU_B_CLR,
       ALU_B_CMP, ALU_B_DRD, ALU_B_DRE, ALU_B_FRD, ALU_B_FRE, ALU_B_LD, ALU_B_LRD, ALU_B_STD, ALU_B_STF,
       ALU_B_UUD, ALU_B_UUF, ALU_B_V, ALU_B_VD, ALU_B_VF, ALU_busy, ALU_free, and_1_out, and_3_out,
       and_4_out, and_5_out, and_6_out, and_7_out, and_8_out, and_9_out, and_10_out, and_11_out, and_12_out,
       and_13_out, and_14_out, and_15_out, and_16_out, and_17_out, and_18_out, and_19_out, and_21_out,
       and_22_out, and_23_out, and_24_out, and_26_out, and_27_out, and_28_out, and_32_out, and_35_out,
       and_36_out, and_37_out, and_38_out, and_39_out, and_41_out, and_42_out, and_43_out, and_44_out,
       and_45_out, and_46_out, and_47_out, and_48_out, and_49_out, and_50_out, and_51_out, and_52_out,
       and_53_out, and_54_out, and_55_out, and_59_out, and_60_out, and_61_out, and_62_out, and_63_out,
       and_64_out, and_65_out, and_66_out, and_67_out, and_68_out, and_69_out, and_70_out, and_71_out,
       and_72_out, and_75_out, and_76_out, and_80_out, and_81_out, and_82_out, and_83_out, and_84_out,
       and_85_out, and_86_out, and_87_out, and_88_out, and_90_out, and_91_out, and_94_out, and_95_out,
       and_100_out, and_106_out, and_107_out, and_108_out, and_109_out, and_110_out, and_111_out,
       and_112_out, and_113_out, and_114_out, and_115_out, and_116_out, and_117_out, and_118_out,
       and_121_out, and_123_out, and_124_out, and_129_out, and_130_out, and_131_out, and_132_out,
       and_133_out, and_134_out, and_137_out, and_138_out, and_139_out, and_140_out, and_142_out,
       and_143_out, and_144_out, and_145_out, and_147_out, and_148_out, and_149_out, and_150_out,
       and_151_out, and_152_out, and_153_out, and_159_out, and_160_out, and_163_out, and_164_out,
       and_165_out, and_169_out, and_174_out, and_176_out, and_177_out, and_178_out, and_179_out,
       and_180_out, and_181_out, and_182_out, and_183_out, and_184_out, and_186_out, and_187_out,
       and_188_out, and_189_out, and_192_out, bitselector_1_out, BTB_JP, BTB_override, C_ct, C_dt, clr,
       clr_ep, clr_sel, clrs_ep, com1, com1_ep, com1_M, com2, com2_ep, comparator_1_eq, comparator_2_eq,
       comparator_3_gt, comparator_4_eq, comparator_5_eq, comparator_6_eq, comparator_7_gt, comparator_8_eq,
       comparator_9_eq, comparator_10_eq, comparator_11_eq, comparator_12_eq, comparator_13_eq,
       comparator_14_eq, comparator_15_eq, comparator_16_eq, comparator_17_eq, comparator_18_gt,
       comparator_18_lt, comparator_19_eq, comparator_20_eq, CT_ALU__LD, CT_ALU__M, CT_ALU__M2, CT_ALU__WD,
       CT_ALU__WF, CT_BLOCK, CT_BUS__DAG, CT_BUS__DAM, CT_BUS__DAR, CT_BUS__DDG, CT_BUS__DDM, CT_BUS__DDR,
       CT_BUS__IAG, CT_BUS__IAR, CT_BUS__IDM, CT_BUS__IDR, CT_CALL__LD, CT_CALLM, CT_DIR__LD, CT_DIR__M,
       CT_DIR__MS, CT_DISP, CT_FL__W1, CT_FL__W2, CT_FU__EPOCH, CT_FU__MF, CT_HALT__LD, CT_INTM, CT_ISCE,
       CT_ISCM, CT_ISS__HALT, CT_ISS__OFL, CT_ISS__OLDB, CT_ISS__ORC, CT_ISS__OSC, CT_ISS__OSTB, CT_ISS__UFL,
       CT_ISS__UMM, CT_ISS__URA, CT_ISS__URB, CT_JPU__JP, CT_JPU__LD, CT_LDB__LD, CT_MB__LD, CT_MB__OFFM,
       CT_MB__ST, CT_MVR, CT_RET__LD, CT_RF__D1, CT_RF__D2, CT_RF__DM, CT_RF__E, CT_RF__FLS, CT_RF__PCAE,
       CT_RF__PCH, CT_RF__PCJ, CT_RF__PCR, CT_RF__PCSE, CT_RF__SCAE, CT_RF__SCD, CT_RF__SCSE, CT_RF__SCSRE,
       CT_RF__SCSS, CT_RF__W1, CT_RF__W2, CT_ROB__EX__E, CT_ROB__FL__STA, CT_ROB__FL__STB, CT_ROB__GEN__STA,
       CT_ROB__GEN__STB, CT_ROB__ST__E, CT_rollback, CT_SC__W1, CT_SC__W2, CT_STB__LD, CT_UBTB, CT_USCB,
       d_ff_1_q, d_ff_16_q, d_ff_17_nq, d_ff_22_q, DC_B_q, dc_e, DC_q, dipswitch_1_out, dipswitch_2_out,
       dipswitch_3_out, dipswitch_4_out, dipswitch_5_out, dipswitch_6_out, dipswitch_7_out, dipswitch_8_out,
       dipswitch_9_out, dipswitch_10_out, dipswitch_11_out, dipswitch_12_out, dipswitch_13_out, DIR_busy,
       DIR_CLR, DIR_free, DIR_LD, DIR_RD, DIR_ST, DIR_V, dp_e, E_t, epoch_DP, epoch_IS, ex_nop, ext_en,
       Fl_JPU, Fl_JPU__EP, Fl_MEM, FL_MEM__EP, ft_e, FT_q, halt_FT_DC_ISS, halted, hlt, id_full,
       id_manager_debug_1_v, inst_comp_1_a_old, inst_comp_2_a_old, inst_comp_3_a_old, inst_comp_4_a_old,
       inst_comp_5_a_old, inst_comp_6_a_old, inst_comp_7_a_old, inst_comp_9_a_old, inst_comp_11_a_old,
       inst_comp_12_a_old, int_accept, int_epoch, INT_HALT, INT_ISS, ISS_B_q, issue, issue_e, issue_e__bf,
       JPU_A__ST, JPU_BTB__J, JPU_BTB__ST, JPU_BTB__V, JPU_CALL, JPU_free, JPU_INT, JPU_JP, JPU_LD, JPU_MF,
       JPU_MFE, JPU_MISS, JPU_RET, kernel_inst, LDB_B__MF, LDB_B__RD, LDB_B__ST, LDB_busy, LDB_forward,
       LDB_ldV, LDB_M__EP, LDB_M__V, load_buffer_debug_1_full, load_buffer_debug_1_mf_o,
       load_buffer_debug_1_v, MB_busy, MB_ep, MB_free, MB_LD, MB_ld__e, MB_LDB__LD, MB_MF, MB_MFE, MB_st__e,
       MB_STB__LD, MB_type__st, MEM_AC, MEM_BF__free, MEM_CLR, MEM_EP, MEM_LD, MEM_LD__CLR, MEM_LD__EP,
       MEM_LD__RD, MEM_LD__REC, MEM_RD, MEM_TYPE__ST, mode, monoflop_1_q, monoflop_2_q, multiplexer_4_out,
       multiplexer_6_out, multiplexer_11_out, multiplexer_13_out, multiplexer_15_out, multiplexer_16_out,
       multiplexer_18_out, multiplexer_19_out, multiplexer_20_out, multiplexer_26_out, multiplexer_34_out,
       multiplexer_35_out, multiplexer_36_out, multiplexer_44_out, multiplexer_48_out, multiplexer_49_out,
       multiplexer_50_out, multiplexer_51_out, multiplexer_53_out, multiplexer_57_out, multiplexer_58_out,
       multiplexer_66_out, nand_11_out, nand_12_out, nor_1_out, nor_2_out, nor_5_out, nor_6_out, nor_8_out,
       nor_9_out, not_2_out, not_3_out, not_7_out, not_8_out, not_10_out, not_11_out, not_12_out, not_13_out,
       not_14_out, not_15_out, not_16_out, not_17_out, not_18_out, not_20_out, not_21_out, not_23_out,
       not_24_out, not_25_out, not_28_out, not_29_out, not_31_out, not_33_out, not_36_out, not_37_out,
       or_2_out, or_3_out, or_5_out, or_6_out, or_7_out, or_8_out, or_17_out, or_19_out, or_20_out,
       or_25_out, or_27_out, or_28_out, or_29_out, or_30_out, or_33_out, or_34_out, or_35_out, or_38_out,
       or_39_out, or_40_out, or_41_out, or_42_out, or_44_out, or_46_out, or_47_out, or_48_out, or_49_out,
       or_50_out, or_51_out, or_52_out, or_53_out, or_54_out, or_56_out, or_57_out, or_58_out, or_59_out,
       or_63_out, or_64_out, or_67_out, PCA, priorityencoder_1_any, register_3_q, register_22_q,
       register_23_q, register_24_q, register_31_q, register_32_q, register_33_q, register_40_q,
       register_45_q, register_57_q, register_64_q, register_69_q, register_73_q, RET_EPOCH, ROB_GEN_DA,
       ROB_GEN_DB, ROB_GEN_INSTA, ROB_GEN_INSTB, rs_ff_1_nq, rs_ff_3_q, rs_ff_4_q, rs_ff_5_nq, rs_ff_5_q,
       rs_ff_6_nq, rs_ff_6_q, rs_ff_7_nq, rs_ff_8_nq, rs_ff_9_nq, rs_ff_10_nq, rs_ff_11_nq, rs_ff_16_q,
       rs_ff_17_q, rs_ff_18_q, rs_ff_19_q, rs_ff_22_nq, rs_ff_as_1_q, RS_full, run_t, STB_busy, STB_M__EP,
       STB_M__V, store_buffer_debug_1_full, sub_1_c_o, V_q, xor_2_out;
  wire [0:0] and_89_out, JPU_BTBPK, keyboard_1_av;
  wire [1:0] and_102_out, and_104_out, and_119_out, and_120_out, bitextender_5_out, bitextender_6_out,
       d_ff_4_q, d_ff_7_q, d_ff_8_q, d_ff_9_q, d_ff_10_q, JPU_BTB__pred, JPU_pred, LDB_M__MD, MB_MD,
       multiplexer_9_out, or_21_out, register_15_q, STB_M__MD;
  wire [1:1] or_18_out, register_43_q, register_67_q;
  wire [2:0] ALU_A_RM, ALU_B_RM, and_92_out, and_96_out, CT_ISS__UFU, CT_RF__MA, CT_RF__MB, CT_RF__SCN,
       CT_RF__WM, CT_SP__MOF, multiplexer_14_out, multiplexer_42_out, nand_1_out, nand_2_out, nand_4_out,
       nand_8_out, not_19_out, not_22_out, register_20_q, register_44_q, store_controller_1_d1_sel,
       store_controller_1_d2_sel, store_controller_2_d1_sel, store_controller_2_d2_sel, undriven;
  wire [2:1] nor_3_out;
  wire [3:0] ALU_A_INST, ALU_B_INST, clr_id, clrs_id, com1_inst, com2_inst, CT_FU__INST, DIR_INST,
       Fl_JPU__INST, FL_MEM__ID, inst_DP, inst_IS, int_inst, LD_id, LDB_B__INST, LDB_M__ID,
       load_buffer_debug_1_id_o, MB_INST, MEM_INST, MEM_LD__INST, multiplexer_2_out, multiplexer_17_out,
       multiplexer_33_out, multiplexer_43_out, multiplexer_52_out, multiplexer_60_out, multiplexer_65_out,
       priorityencoder_1_num, register_2_q, register_21_q, register_30_q, register_39_q, register_63_q,
       RET_INST, ROB_FL_INSTA, ROB_FL_INSTB, STB_M__ID;
  wire [4:0] CT_ISS__RA, CT_ISS__RB, CT_ISS__RC, CT_RF__RA, CT_RF__RB, CT_RF__WS;
  wire [6:5] undriven_2;
  wire [6:6] and_185_out;
  wire [7:0] ALU_A_F, ALU_A_FI, ALU_A_T__F, ALU_B_F, ALU_B_FI, ALU_B_T__F, bitextender_2_out, byte_D0,
       byte_D0_iv, byte_D1, byte_D2, byte_D3, byte_I0, byte_I0_iv, byte_I1, byte_I2, byte_I3, counter_3_out,
       CT_FL__D1, CT_FL__D2, CT_FU__WR, CT_RF__R1, CT_RF__R2, DIR_WR, fl_i, FU_free, LDB_B__WR,
       load_buffer_debug_1_wr_o, MB_WR, multiplexer_5_out, multiplexer_23_out, multiplexer_25_out,
       multiplexer_39_out, multiplexer_41_out, multiplexer_46_out, multiplexer_55_out, register_27_q,
       register_29_q, register_36_q, register_38_q, register_42_q, register_66_q, ROB_FL_A, ROB_FL_B,
       ROB_GEN_WA, ROB_GEN_WB, xor_3_out;
  wire [7:2] FU_F__V;
  wire [7:3] ALU_A_WR, ALU_B_WR, FU_D__V;
  wire [8:0] ALU_A_CT, ALU_B_CT, CT_ALU__CT, multiplexer_24_out, multiplexer_40_out, register_28_q,
       register_37_q;
  wire [9:0] and_40_out;
  wire [15:0] and_166_out, and_168_out, and_170_out, and_171_out, and_173_out, bitextender_3_out,
       bitextender_4_out, bitextender_7_out, bitextender_9_out, bitextender_10_out, clr_16, clrs_16,
       d_ff_19_q, demultiplexer_1_out_0, demultiplexer_2_out_0, icmk_16, icmks_16, id_manager_debug_1_c16,
       id_manager_debug_1_cm1, id_manager_debug_1_cm2, id_manager_debug_1_us, id_manager_debug_1_vv1,
       id_manager_debug_1_vv2, keyboard_1_d, multiplexer_31_out, multiplexer_69_out, not_34_out, not_35_out,
       or_60_out, or_61_out, or_62_out, register_51_q, register_87_q, register_91_q, register_92_q, V1_inst,
       V2_inst;
  wire [16:0] rom_1_d;
  wire [31:0] A_q, add_1_s, add_4c32_1_s, add_4c32_2_s, add_4c32_3_s, addsub_4c32_1_s, alu_32_1_p8,
       alu_32_1_p11, alu_32_1_p12, alu_32_1_p14, ALU_A_A, ALU_A_B, ALU_A_R, ALU_A_T__R, ALU_B_A, ALU_B_B,
       ALU_B_R, ALU_B_T__R, bitextender_1_out, counter_1_out, counter_2_out, CT_RF__DR, CT_SC__D1, CT_SC__D2,
       CT_SC__FD, d_ff_18_q, D_q, DIR, FL, HALT_PC, I_A__R_q, I_D__R_q, int_pc, int_vec_t, ISC, ISC_i,
       JPU_ADDR, JPU_BTB__tar, JPU_PC, LD_addr, LDB_B__D, LDB_ldD, LDB_M__A, MB_addr, MB_data, MB_PC,
       MEM_FPC, MEM_LD__D, multiplexer_3_out, multiplexer_7_out, multiplexer_8_out, multiplexer_12_out,
       multiplexer_21_out, multiplexer_22_out, multiplexer_27_out, multiplexer_28_out, multiplexer_29_out,
       multiplexer_30_out, multiplexer_32_out, multiplexer_37_out, multiplexer_38_out, multiplexer_45_out,
       multiplexer_54_out, multiplexer_59_out, multiplexer_62_out, multiplexer_64_out, multiplexer_67_out,
       multiplexer_68_out, mVec, pc_read, pc_ret__int, pca_i, PCS, PCS_DC, PCS_FT, pcs_i, R_A, R_B,
       ramdualaccess_1_d1, ramdualaccess_1_d2, register_7_q, register_8_q, register_14_q, register_16_q,
       register_25_q, register_26_q, register_34_q, register_35_q, register_41_q, register_50_q,
       register_65_q, register_86_q, SCA, sca_i, SCS, STB_M__A, STB_M__D;
  wire [31:24] res_station_debug_1_disp_32;
  wire [36:0] and_167_out, bitextender_8_out, BTB_D_q, BTB_DP, BTB_fetch, BTB_pack__iss, BTB_packet;

  Comparator #(.Bits(32)) comparator_1 (.a(PCS), .b(32'h40), .eq(comparator_1_eq));  // open: gt, lt
  Comparator #(.Bits(32)) comparator_2 (.a(PCS), .b(32'h58), .eq(comparator_2_eq));  // open: gt, lt
  RS_FF_AS rs_ff_as_1 (.S(run_t), .R(dipswitch_1_out), .Q(rs_ff_as_1_q));  // open: nQ
  DipSwitch dipswitch_1 (.out(dipswitch_1_out));
  LED led_1 (.in(comparator_1_eq));
  LED led_2 (.in(comparator_2_eq));
  DipSwitch #(.dipDefault("true")) dipswitch_2 (.out(dipswitch_2_out));
  DipSwitch dipswitch_3 (.out(dipswitch_3_out));
  // Probe E on E_t
  // Probe R on run_t
  // Probe issue_e on issue_e
  // Probe CT_ISS-_OLDB on CT_ISS__OLDB
  // Probe clr on clr
  // Probe issue_32 on {byte_I0, byte_I1, byte_I2, byte_I3}
  // Probe disp_32 on {byte_D0, byte_D1, byte_D2, byte_D3}
  // Probe on com1
  // Probe on com2
  // Probe on com1_inst
  // Probe on com2_inst
  // Probe on epoch_IS
  // Probe on inst_IS
  Comparator #(.Bits(32)) comparator_3 (.a(counter_1_out), .b(32'h50), .gt(comparator_3_gt));  // open: eq, lt
  Comparator #(.Bits(32)) comparator_4 (.a(counter_1_out), .b(32'hc), .eq(comparator_4_eq));  // open: gt, lt
  Comparator #(.Bits(32)) comparator_5 (.a(counter_1_out), .b(32'h14), .eq(comparator_5_eq));  // open: gt, lt
  Comparator #(.Bits(32)) comparator_6 (.a(counter_1_out), .b(32'h16), .eq(comparator_6_eq));  // open: gt, lt
  Counter #(.Bits(32)) counter_1 (
    .en(dipswitch_2_out), .C(C_dt), .clr(dipswitch_3_out), .out(counter_1_out));  // open: ovf
  Counter #(.Bits(32)) counter_2 (
    .en(rs_ff_as_1_q), .C(C_dt), .clr(dipswitch_1_out), .out(counter_2_out));  // open: ovf
  // Probe cycle on counter_1_out
  // Probe Ecycle on counter_2_out
  PullDown #(.Bits(32)) pulldown_1 (.out(I_A__bus));
  RS_FF_AS rs_ff_as_2 (.S(comparator_4_eq), .R(dipswitch_4_out), .Q(E_t));  // open: nQ
  DipSwitch dipswitch_4 (.out(dipswitch_4_out));
  RS_FF_AS rs_ff_as_3 (.S(comparator_5_eq), .R(comparator_6_eq), .Q(run_t));  // open: nQ
  LED led_3 (.in(MB_ld__e));
  LED led_4 (.in(MB_st__e));
  DipSwitch dipswitch_5 (.out(dipswitch_5_out));
  DipSwitch dipswitch_6 (.out(dipswitch_6_out));
  Multiplexer multiplexer_1 (.sel(dipswitch_5_out), .in_0(dipswitch_6_out), .in_1(C), .out(C_dt));
  not not_1 (C_ct, C_dt);
  not not_2 (not_2_out, I_valid);
  assign CT_BUS__IDM = not_2_out ? 1'b1 : 1'bz;  // Driver driver_1
  and and_1 (and_1_out, I_valid, ft_e);
  assign CT_RF__PCSE = and_1_out ? 1'b1 : 1'bz;  // Driver driver_2
  assign CT_BUS__IAR = and_1_out ? 1'b1 : 1'bz;  // Driver driver_3
  assign CT_BUS__IAG = ft_e ? 1'b1 : 1'bz;  // Driver driver_4
  assign I_LD = ft_e ? 1'b1 : 1'bz;  // Driver driver_5
  not not_3 (not_3_out, clr_sel);
  Comparator #(.Bits(32)) comparator_7 (.a(PCS), .b(mVec), .gt(comparator_7_gt));  // open: eq, lt
  BitExtender #(.inputBits(16), .outputBits(32)) bitextender_1 (.in({byte_D2, byte_D3}), .out(bitextender_1_out));
  RS_FF rs_ff_1 (.S(INT_out), .C(C_dt), .R(CT_INTM), .nQ(rs_ff_1_nq));  // open: Q
  and and_2 (INT_out, rs_ff_1_nq, int_accept);
  and and_3 (and_3_out, FL[14], INT_nor);
  and and_4 (and_4_out, halted, INT_nor);
  PullDown pulldown_2 (.out(CT_ISCM));
  PullDown pulldown_3 (.out(CT_ISCE));
  PullDown pulldown_4 (.out(JPU_INT));
  Register #(.Bits(32)) u_ISC (.D(ISC_i), .C(C_dt), .en(CT_ISCE), .Q(ISC));
  Register #(.Bits(32)) register_1 (.D(INT_vec), .C(C_dt), .en(int_accept), .Q(int_vec_t));
  PullDown #(.Bits(32)) pulldown_5 (.out(D_A__bus));
  LED led_5 (.in(CT_JPU__LD));
  LED led_6 (.in(D_ST));
  LED led_7 (.in(JPU_BTB__ST));
  LED led_8 (.in(Fl_MEM));
  LED led_9 (.in(epoch_IS));
  // Probe ID on inst_DP
  id_manager_debug id_manager_debug_1 (
    .C(C_ct), .\use (issue), .S1_inst(V1_inst), .S2_inst(V2_inst), .clr(clr), .clr_self(not_3_out),
    .clr_ep(clr_ep), .clr_id(clr_id), .epoch(epoch_IS), .id(inst_IS), .V(id_manager_debug_1_v), .com1(com1),
    .com1_id(com1_inst), .com1_ep(com1_ep), .com2(com2), .com2_id(com2_inst), .com2_ep(com2_ep),
    .ext_en(ext_en), .cmk_16(icmk_16), .clr_16(clr_16), .cmks_16(icmks_16), .clrs_16(clrs_16),
    .VV1(id_manager_debug_1_vv1), .VV2(id_manager_debug_1_vv2), .US(id_manager_debug_1_us),
    .CM1(id_manager_debug_1_cm1), .CM2(id_manager_debug_1_cm2), .C16(id_manager_debug_1_c16));
  flush_mux flush_mux_1 (
    .M_v(Fl_MEM), .M_id(FL_MEM__ID), .M_ep(FL_MEM__EP), .J_v(Fl_JPU), .J_id(Fl_JPU__INST), .J_ep(Fl_JPU__EP),
    .I_v(INT_out), .I_id(com2_inst), .I_ep(com2_ep), .sel(clr_sel), .m_v_2(clr), .m_id_2(clr_id),
    .m_ep_2(clr_ep));
  Comparator #(.Bits(4)) comparator_8 (.a(register_2_q), .b(com1_inst), .eq(comparator_8_eq));  // open: gt, lt
  Comparator #(.Bits(4)) comparator_9 (.a(register_2_q), .b(com2_inst), .eq(comparator_9_eq));  // open: gt, lt
  Register #(.Bits(4)) register_2 (.D(CT_FU__INST), .C(C_ct), .en(CT_HALT__LD), .Q(register_2_q));
  Register register_3 (.D(CT_FU__EPOCH), .C(C_ct), .en(CT_HALT__LD), .Q(register_3_q));
  Add #(.Bits(32)) add_1 (.a(R_A), .b(bitextender_1_out), .c_i(1'b0), .s(add_1_s));  // open: c_o
  Comparator #(.Bits(6)) comparator_10 (.a(D_A__bus[31:26]), .b({6{1'b0}}), .eq(comparator_10_eq));  // open: gt, lt
  Comparator #(.Bits(6)) comparator_11 (.a(I_A__bus[31:26]), .b({6{1'b0}}), .eq(comparator_11_eq));  // open: gt, lt
  // Probe on CT_RF__WS
  // Probe on CT_RF__WM
  // Probe on CT_RF__RA
  // Probe on CT_RF__MA
  // Probe on CT_RF__RB
  // Probe on CT_RF__MB
  and and_5 (and_5_out, com1, comparator_8_eq);
  and and_6 (and_6_out, com2, comparator_9_eq);
  and and_7 (and_7_out, 1'b0, ~comparator_7_gt);  // And
  D_FF d_ff_1 (.D(INT_out), .C(C_ct), .Q(d_ff_1_q));  // open: nQ
  or or_1 (int_accept, and_3_out, and_4_out, INT_nmk);
  Comparator #(.Bits(6)) comparator_12 (.a(D_A__bus[31:26]), .b(6'b000010), .eq(comparator_12_eq));  // open: gt, lt
  and and_8 (and_8_out, comparator_10_eq, D_LD);
  and and_9 (and_9_out, D_ST, comparator_10_eq);
  and and_10 (and_10_out, comparator_11_eq, I_LD);
  Comparator #(.Bits(30)) comparator_13 (.a(D_A__bus[31:2]), .b(30'h1000000), .eq(comparator_13_eq));  // open: gt, lt
  Comparator #(.Bits(30)) comparator_14 (.a(D_A__bus[31:2]), .b(30'h1000001), .eq(comparator_14_eq));  // open: gt, lt
  Comparator #(.Bits(30)) comparator_15 (.a(D_A__bus[31:2]), .b(30'h1000002), .eq(comparator_15_eq));  // open: gt, lt
  Comparator #(.Bits(30)) comparator_16 (.a(D_A__bus[31:2]), .b(30'h1000003), .eq(comparator_16_eq));  // open: gt, lt
  DipSwitch dipswitch_7 (.out(dipswitch_7_out));
  DipSwitch dipswitch_8 (.out(dipswitch_8_out));
  LED led_10 (.in(halt_FT_DC_ISS));
  LED led_11 (.in(clr));
  LED led_12 (.in(LDB_B__RD));
  // Probe FU on FU_free
  // Probe INST on {byte_I0, byte_I1, byte_I2, byte_I3}
  // Probe INST on {byte_D0, byte_D1, byte_D2, byte_D3}
  or or_2 (or_2_out, run_t, INT_out);
  not not_4 (id_full, id_manager_debug_1_v);
  or or_3 (or_3_out, and_5_out, and_6_out);
  inst_comp inst_comp_1 (
    .A_id(register_2_q), .A_ep(register_3_q), .B_id(clr_id), .B_ep(clr_ep), .A_old(inst_comp_1_a_old));
  RS_FF u_mode (.S(and_7_out), .C(C_dt), .R(comparator_7_gt), .Q(mode));  // open: nQ
  Register #(.Bits(32)) MVR (.D(add_1_s), .C(C_dt), .en(CT_MVR), .Q(mVec));
  RS_FF rs_ff_2 (.S(INT_out), .C(C_ct), .R(INT_ISS), .Q(INT_HALT));  // open: nQ
  RS_FF rs_ff_3 (.S(d_ff_1_q), .C(C_ct), .R(INT_ISS), .Q(rs_ff_3_q));  // open: nQ
  Comparator #(.Bits(4)) comparator_17 (.a(inst_IS), .b(com1_inst), .eq(comparator_17_eq));  // open: gt, lt
  assign issue = INT_ISS ? 1'b1 : 1'bz;  // Driver driver_6
  assign CT_JPU__LD = INT_ISS ? 1'b1 : 1'bz;  // Driver driver_7
  assign JPU_INT = INT_ISS ? 1'b1 : 1'bz;  // Driver driver_8
  assign CT_ISS__OSTB = INT_ISS ? 1'b1 : 1'bz;  // Driver driver_9
  Register #(.Bits(32)) register_4 (.D(PCS_DC), .C(C_dt), .en(INT_ISS), .Q(int_pc));
  Register #(.Bits(4)) register_5 (.D(inst_IS), .C(C_ct), .en(INT_ISS), .Q(int_inst));
  Register register_6 (.D(epoch_IS), .C(C_ct), .en(INT_ISS), .Q(int_epoch));
  and and_11 (and_11_out, comparator_12_eq, D_LD);
  and and_12 (and_12_out, D_ST, comparator_12_eq);
  and and_13 (and_13_out, D_LD, comparator_13_eq);
  and and_14 (and_14_out, D_LD, comparator_14_eq);
  and and_15 (and_15_out, D_ST, C_dt, comparator_15_eq);
  and and_16 (and_16_out, D_ST, comparator_16_eq);
  LED led_13 (.in(LDB_B__ST));
  LED led_14 (.in(JPU_CALL));
  and and_17 (and_17_out, JPU_CALL, dipswitch_7_out);
  LED led_15 (.in(CT_RET__LD));
  and and_18 (and_18_out, CT_RET__LD, dipswitch_8_out);
  LED led_16 (.in(LDB_forward));
  assign byte_I0_iv = ~byte_I0;  // Not not_5, 8 bits wide
  assign byte_D0_iv = ~byte_D0;  // Not not_6, 8 bits wide
  nor nor_1 (nor_1_out, clr, hlt);
  and and_19 (and_19_out, rs_ff_4_q, or_3_out);
  DipSwitch dipswitch_9 (.out(dipswitch_9_out));
  RAMDualAccess #(.AddrBits(24), .isProgramMemory("true"), .Bits(32)) ramdualaccess_1 (
    .str(and_9_out), .C(C_dt), .ld(1'b1), .A1(D_A__bus[25:2]), .Din1(D_D__bus), .A2(I_A__bus[25:2]),
    .D1(ramdualaccess_1_d1), .D2(ramdualaccess_1_d2));
  Counter #(.Bits(8)) counter_3 (.en(1'b1), .C(and_15_out), .clr(1'b0), .out(counter_3_out));  // open: ovf
  // Probe inst on {byte_I0, byte_I1, byte_I2, byte_I3}
  // Probe R_A on R_A
  // Probe R_B on R_B
  // Probe PC on PCS
  // Probe SCS on SCS
  // Probe SCA on SCA
  // Probe FL on FL
  // Probe CT_BUS-_IDM on CT_BUS__IDM
  // Probe C_i on C_dt
  Monoflop monoflop_1 (.C(and_17_out), .R(dipswitch_10_out), .Q(monoflop_1_q));  // open: nQ
  DipSwitch dipswitch_10 (.out(dipswitch_10_out));
  Monoflop monoflop_2 (.C(and_18_out), .R(dipswitch_11_out), .Q(monoflop_2_q));  // open: nQ
  DipSwitch dipswitch_11 (.out(dipswitch_11_out));
  Register #(.Bits(32)) D (.D(D_D__bus), .C(C_dt), .en(D_ST), .Q(D_q));
  Register #(.Bits(32)) A (.D(D_A__bus), .C(C_dt), .en(D_ST), .Q(A_q));
  RS_FF FT (.S(or_2_out), .C(C_ct), .R(hlt), .Q(FT_q), .nQ(halted));
  not not_7 (not_7_out, halt_FT_DC_ISS);
  and and_20 (INT_ISS, rs_ff_3_q, ~comparator_17_eq, ~STB_busy);  // And
  GraphicCard #(.graphicHeight(90), .Bits(32)) graphiccard_1 (
    .A(D_A__bus[16:2]), .str(and_12_out), .C(C_dt), .ld(and_11_out), .B(dipswitch_9_out), .D(D_D__bus));
  assign D_D__bus = and_8_out ? ramdualaccess_1_d1 : 32'bz;  // Driver driver_10
  assign I_D__bus = and_10_out ? ramdualaccess_1_d2 : 32'bz;  // Driver driver_11
  ROM #(.AddrBits(8), .Bits(17)) rom_1 (.A(counter_3_out), .sel(1'b1), .D(rom_1_d));
  Keyboard keyboard_1 (.C(and_15_out), .en(1'b1), .D(keyboard_1_d), .av(keyboard_1_av[0]));
  Terminal terminal_1 (.D(D_D__bus), .C(C_dt), .en(and_16_out));
  Break #(.Cycles(1000000)) A_2 (.brk(monoflop_1_q));
  Break #(.Cycles(1000000)) A_3 (.brk(monoflop_2_q));
  // Probe on D_q
  // Probe on A_q
  and and_21 (and_21_out, nor_1_out, FT_q);
  // Probe V1_inst on V1_inst
  // Probe VG1_inst on id_manager_debug_1_vv1
  // Probe V2_inst on V2_inst
  // Probe VG2_inst on id_manager_debug_1_vv2
  // Probe U_inst on id_manager_debug_1_us
  // Probe CLR_inst on id_manager_debug_1_c16
  // Probe CM2_inst on id_manager_debug_1_cm2
  // Probe CM1_inst on id_manager_debug_1_cm1
  assign hlt = and_19_out ? 1'b1 : 1'bz;  // Driver driver_12
  assign CT_RF__PCH = and_19_out ? 1'b1 : 1'bz;  // Driver driver_13
  Register #(.Bits(32)) register_7 (.D(pc_read), .C(C_dt), .en(CT_HALT__LD), .Q(register_7_q));
  and and_22 (and_22_out, inst_comp_1_a_old, ~CT_HALT__LD);  // And
  D_FF d_ff_2 (.D(INT_ISS), .C(C_ct), .Q(CT_INTM));  // open: nQ
  Register #(.Bits(32)) register_8 (.D(D_D__bus), .C(C_dt), .en(and_12_out), .Q(register_8_q));
  and and_23 (and_23_out, comparator_3_gt, ~rom_1_d[16]);  // And
  and and_24 (and_24_out, nor_1_out, FT_q);
  Register DC (.D(and_24_out), .C(C_ct), .en(1'b1), .Q(DC_q));
  and and_25 (ft_e, FT_q, not_7_out);
  Register DC_B (.D(and_21_out), .C(C_dt), .en(1'b1), .Q(DC_B_q));
  Register #(.Bits(32)) register_9 (.D(PCS), .C(C_dt), .en(CT_RF__PCSE), .Q(PCS_FT));
  // Probe on register_8_q
  assign D_D__bus = and_13_out ? {{16{1'b0}}, keyboard_1_d} : 32'bz;  // Driver driver_14
  assign D_D__bus = and_14_out ? {{31{1'b0}}, keyboard_1_av[0]} : 32'bz;  // Driver driver_15
  // Probe com1 on com1
  // Probe com2 on com2
  // Probe com1_inst on com1_inst
  // Probe com2_inst on com2_inst
  // Probe PC_inst on inst_IS
  and and_26 (and_26_out, nor_1_out, DC_B_q);
  and and_27 (and_27_out, DC_B_q, not_7_out);
  DipSwitch dipswitch_12 (.out(dipswitch_12_out));
  Sub #(.Bits(4)) sub_1 (.a(clr_id), .b(4'b0000), .c_i(not_8_out), .s(clrs_id), .c_o(sub_1_c_o));
  not not_8 (not_8_out, clr_sel);
  D_FF #(.Bits(32)) d_ff_3 (.D(register_7_q), .C(C_ct), .Q(HALT_PC));  // open: nQ
  RS_FF rs_ff_4 (.S(CT_HALT__LD), .C(C_ct), .R(and_22_out), .Q(rs_ff_4_q));  // open: nQ
  assign MB_LD = CT_INTM ? 1'b1 : 1'bz;  // Driver driver_16
  assign CT_MB__ST = CT_INTM ? 1'b1 : 1'bz;  // Driver driver_17
  assign CT_FU__INST = CT_INTM ? int_inst : 4'bz;  // Driver driver_18
  assign CT_FU__EPOCH = CT_INTM ? int_epoch : 1'bz;  // Driver driver_19
  assign CT_ISCM = CT_INTM ? 1'b1 : 1'bz;  // Driver driver_20
  assign CT_ISCE = CT_INTM ? 1'b1 : 1'bz;  // Driver driver_21
  assign CT_RF__SCD = CT_INTM ? 1'b1 : 1'bz;  // Driver driver_22
  assign CT_RF__SCN = CT_INTM ? 3'b100 : 3'bz;  // Driver driver_23
  and and_28 (and_28_out, nor_1_out, DC_q);
  Register ISS (.D(and_28_out), .C(C_ct), .en(1'b1), .Q(dp_e));
  and and_29 (dc_e, DC_q, not_7_out);
  Register ISS_B (.D(and_26_out), .C(C_dt), .en(1'b1), .Q(ISS_B_q));
  Register #(.Bits(32)) register_10 (.D(PCS_FT), .C(C_dt), .en(CT_RF__PCSE), .Q(PCS_DC));
  or or_4 (halt_FT_DC_ISS, id_full, RS_full, INT_HALT, dipswitch_13_out, dipswitch_12_out, LDB_busy, STB_busy);
  DipSwitch dipswitch_13 (.out(dipswitch_13_out));
  xor xor_1 (clrs_ep, clr_ep, sub_1_c_o);
  and and_30 (issue_e__bf, ISS_B_q, not_7_out);
  PullDown pulldown_6 (.out(CT_DISP));
  PullDown pulldown_7 (.out(CT_rollback));
  PullDown pulldown_8 (.out(com2));
  PullDown #(.Bits(4)) pulldown_9 (.out(com2_inst));
  PullDown pulldown_10 (.out(com1_M));
  PullDown pulldown_11 (.out(com1));
  PullDown #(.Bits(4)) pulldown_12 (.out(com1_inst));
  and and_31 (issue_e, dp_e, not_7_out);
  BTB btb_1 (
    .C(C_dt), .E(JPU_BTB__ST), .V_in(1'b1), .id(JPU_PC[5:2]), .tag(JPU_PC[17:6]), .pred(JPU_pred),
    .tar(JPU_ADDR), .R_id(PCS[5:2]), .R_tag(PCS[17:6]), .V(BTB_packet[1]), .J(BTB_JP),
    .pred_O(BTB_packet[4:3]), .tar_O(BTB_packet[36:5]));
  Multiplexer #(.Bits(4)) multiplexer_2 (.sel(com2), .in_0(com1_inst), .in_1(com2_inst), .out(multiplexer_2_out));
  or or_5 (or_5_out, MEM_AC, MEM_CLR);
  not not_9 (MEM_LD__REC, LDB_forward);
  inst_comp inst_comp_2 (.A_id(MEM_INST), .A_ep(MEM_EP), .B_id(clrs_id), .B_ep(clrs_ep), .A_old(inst_comp_2_a_old));
  inst_comp inst_comp_3 (
    .A_id(MEM_LD__INST), .A_ep(MEM_LD__EP), .B_id(clrs_id), .B_ep(clrs_ep), .A_old(inst_comp_3_a_old));
  D_FF #(.Bits(2)) d_ff_4 (.D({LDB_M__V, STB_M__V}), .C(C_ct), .Q(d_ff_4_q));  // open: nQ
  and and_32 (and_32_out, ~MEM_LD, or_5_out);  // And
  // ROB_gen rob_gen_1: pin names not known; wires that end beside it: C_dt, CT_ROB__GEN__STA, CT_ROB__GEN__STB, ROB_GEN_DA, ROB_GEN_DB, ROB_GEN_WA, ROB_GEN_WB, ROB_GEN_INSTA, ROB_GEN_INSTB, com1, com2, com1_inst, com2_inst, clr_16, RET_INST, CT_RF__D1, CT_RF__R1, CT_RF__W1, CT_RF__D2, CT_RF__R2, CT_RF__W2, CT_RF__DR
  ROB_PC rob_pc_1 (
    .C(C_dt), .E(issue), .D(PCS_DC), .inst(inst_IS), .com_id(multiplexer_2_out), .read_id(inst_DP),
    .ret_id(RET_INST), .D1(pca_i), .D2(pc_read), .D3(pc_ret__int));
  ROB_SC rob_sc_1 (
    .C(C_dt), .E(CT_RF__SCSRE), .D(ISC_i), .inst(inst_DP), .com1(com1), .com2(com2), .com1_id(com1_inst),
    .com2_id(com2_inst), .clr_16(clr_16), .roll(clr_id), .SCA(SCA), .W1(CT_SC__W1), .D1(CT_SC__D1),
    .W2(CT_SC__W2), .D2(CT_SC__D2), .D3(CT_SC__FD));
  DipSwitch dipswitch_14 (.out(BTB_packet[0]));
  or or_6 (or_6_out, multiplexer_6_out, MEM_BF__free);
  or or_7 (or_7_out, d_ff_4_q[0], d_ff_4_q[1], MEM_CLR);
  RS_FF rs_ff_5 (.S(MEM_LD), .C(C_ct), .R(and_32_out), .Q(rs_ff_5_q), .nQ(rs_ff_5_nq));
  and and_33 (MEM_CLR, inst_comp_2_a_old, ~MEM_TYPE__ST, clr);  // And
  and and_34 (MEM_LD__CLR, inst_comp_3_a_old, clr);
  and and_35 (and_35_out, byte_D0[3], byte_D0[0]);
  and and_36 (and_36_out, byte_D0[2], byte_D0[0]);
  and and_37 (and_37_out, byte_D0_iv[3], byte_D0_iv[2], byte_D0[1], byte_D0_iv[0]);
  and and_38 (and_38_out, byte_D0_iv[4], byte_D0[3], byte_D0[2], byte_D0[1]);
  and and_39 (and_39_out, byte_D0[4], byte_D0_iv[3], byte_D0_iv[2], byte_D0[1], byte_D0[0]);
  and and_40 (and_40_out[7], byte_D0_iv[4], byte_D0[3], byte_D0[2]);
  and and_41 (and_41_out, byte_D0[4], byte_D0[2], byte_D0_iv[1]);
  and and_42 (and_42_out, byte_D0[4], byte_D0_iv[3], byte_D0_iv[2]);
  and and_43 (and_43_out, byte_D0_iv[4], byte_D0_iv[3], byte_D0_iv[2]);
  and and_44 (and_44_out, byte_D0_iv[4], byte_D0_iv[3]);
  and and_45 (and_45_out, byte_D0_iv[4], byte_D0[3], byte_D0_iv[2], byte_D0_iv[1]);
  and and_46 (and_46_out, byte_D0_iv[4], byte_D0[3], byte_D0_iv[2]);
  and and_47 (and_47_out, byte_D0[4], byte_D0[3]);
  and and_48 (and_48_out, byte_D0_iv[4], byte_D0_iv[3], byte_D0[2], byte_D0_iv[1]);
  and and_49 (and_49_out, byte_D0[4], byte_D0[2], byte_D0[1]);
  and and_50 (and_50_out, byte_D0_iv[4], byte_D0_iv[3], byte_D0_iv[2], byte_D0[1], byte_D0[0]);
  and and_51 (and_51_out, byte_D0_iv[2], byte_D0_iv[0]);
  and and_52 (and_52_out, byte_D0[2], byte_D0[0]);
  and and_53 (and_53_out, byte_D0[1], byte_D0[2], byte_D0[4]);
  and and_54 (and_54_out, byte_D0[3], byte_D0[4]);
  and and_55 (and_55_out, ~clr_sel, clr);  // And
  not not_10 (not_10_out, MEM_CLR);
  not not_11 (not_11_out, B_used);
  not not_12 (not_12_out, MEM_CLR);
  not not_13 (not_13_out, B_used);
  and and_56 (MEM_AC, or_6_out, D_accept, not_10_out, not_11_out);
  and and_57 (MEM_RD, not_12_out, not_13_out, rs_ff_5_q);
  or or_8 (or_8_out, rs_ff_5_nq, MEM_AC, MEM_CLR);
  or or_9 (and_40_out[9], and_35_out, and_36_out, and_37_out);
  or or_10 (and_40_out[6], and_41_out, and_38_out, and_39_out);
  or or_11 (and_40_out[5], and_40_out[7], and_41_out, and_42_out);
  or or_12 (and_40_out[4], and_48_out, and_49_out, and_43_out);
  or or_13 (and_40_out[3], and_44_out, and_49_out, and_45_out);
  or or_14 (and_40_out[2], and_46_out, and_47_out);
  or or_15 (and_40_out[1], and_48_out, and_49_out, and_50_out);
  or or_16 (and_40_out[0], byte_D0[3], byte_D0[1], and_51_out, and_52_out);
  nor nor_2 (nor_2_out, and_53_out, and_54_out);
  assign CT_RF__PCSE = and_55_out ? 1'b1 : 1'bz;  // Driver driver_24
  assign CT_RF__PCJ = and_55_out ? 1'b1 : 1'bz;  // Driver driver_25
  Multiplexer #(.Bits(32)) multiplexer_3 (.sel(CT_RF__PCH), .in_0(MEM_FPC), .in_1(HALT_PC), .out(multiplexer_3_out));
  xor xor_2 (xor_2_out, STB_M__EP, LDB_M__EP);
  Comparator #(.Bits(4)) comparator_18 (
    .a(LDB_M__ID), .b(STB_M__ID), .gt(comparator_18_gt), .lt(comparator_18_lt));  // open: eq
  and and_58 (MEM_LD, or_7_out, or_8_out);
  nor nor_3 (nor_3_out[1], byte_D1[1], nor_3_out[2]);
  nor nor_4 (nor_3_out[2], byte_D1[0], byte_D1[1], byte_D1[2]);
  and and_59 (and_59_out, byte_D0_iv[7], byte_D0_iv[6], byte_D0[5]);
  and and_60 (and_60_out, byte_D0_iv[7], byte_D0[6], byte_D0_iv[5]);
  and and_61 (and_61_out, STB_M__V, LDB_M__V);
  Multiplexer multiplexer_4 (
    .sel(xor_2_out), .in_0(comparator_18_gt), .in_1(comparator_18_lt), .out(multiplexer_4_out));
  and and_62 (and_62_out, MEM_AC, MEM_RD, not_14_out, not_15_out);
  not not_14 (not_14_out, MEM_TYPE__ST);
  not not_15 (not_15_out, MEM_LD__CLR);
  or or_17 (or_17_out, MEM_LD__REC, MEM_LD__CLR);
  and and_63 (and_63_out, byte_D0_iv[0], byte_D0_iv[1], byte_D0[2], byte_D0[3], byte_D0[4], byte_D0_iv[5], byte_D0_iv[6], byte_D0_iv[7]);
  and and_64 (and_64_out, byte_D0[1], byte_D0_iv[2], byte_D0[3], byte_D0[4], byte_D0_iv[5], byte_D0_iv[6], byte_D0_iv[7]);
  not not_16 (not_16_out, byte_D0[0]);
  and and_65 (and_65_out, byte_D0[1], byte_D0[2], byte_D0[3], byte_D0[4], byte_D0_iv[5], byte_D0_iv[6], byte_D0_iv[7]);
  or or_18 (or_18_out[1], byte_D1[1], byte_D1[2], byte_D1[0]);
  or or_19 (or_19_out, and_60_out, and_59_out);
  and and_66 (and_66_out, com1, CT_RF__W1);
  and and_67 (and_67_out, com2, CT_RF__W2);
  ROB_FL rob_fl_1 (
    .C(C_dt), .E1(CT_ROB__FL__STA), .E2(CT_ROB__FL__STB), .D1(ROB_FL_A), .D2(ROB_FL_B), .inst1(ROB_FL_INSTA),
    .inst2(ROB_FL_INSTB), .com1(com1), .com2(com2), .com1_id(com1_inst), .com2_id(com2_inst),
    .clr_16(clr_16), .W1_O(CT_FL__W1), .D1_O(CT_FL__D1), .W2_O(CT_FL__W2), .D2_O(CT_FL__D2));
  add_4c32 add_4c32_1 (.a(multiplexer_3_out), .b(4'b0100), .s(add_4c32_1_s));  // open: c
  Multiplexer #(.Bits(8)) multiplexer_5 (
    .sel(CT_BUS__IDM), .in_0(I_D__bus[31:24]), .in_1(8'h72), .out(multiplexer_5_out));
  Multiplexer multiplexer_6 (.sel(and_61_out), .in_0(STB_M__V), .in_1(multiplexer_4_out), .out(multiplexer_6_out));
  and and_68 (and_68_out, byte_D0[4], byte_D0[3], byte_D0_iv[1], byte_D0_iv[2], byte_D0_iv[5], byte_D0_iv[6], byte_D0_iv[7]);
  or or_20 (or_20_out, and_63_out, and_64_out);
  and and_69 (and_69_out, BTB_JP, ~CT_RF__PCJ);  // And
  Multiplexer #(.Bits(32)) multiplexer_7 (
    .sel(and_55_out), .in_0(JPU_ADDR), .in_1(add_4c32_1_s), .out(multiplexer_7_out));
  not not_17 (not_17_out, multiplexer_6_out);
  Multiplexer #(.Bits(32)) multiplexer_8 (
    .sel(multiplexer_6_out), .in_0(LDB_M__A), .in_1(STB_M__A), .out(multiplexer_8_out));
  Multiplexer #(.Bits(2)) multiplexer_9 (
    .sel(multiplexer_6_out), .in_0(LDB_M__MD), .in_1(STB_M__MD), .out(multiplexer_9_out));
  and and_70 (and_70_out, or_17_out, ~and_62_out);  // And
  and and_71 (and_71_out, and_65_out, byte_D0[0]);
  and and_72 (and_72_out, not_16_out, and_65_out);
  // regFile4 regfile4_1: pin names not known; wires that end beside it: C_dt, and_66_out, and_67_out, CT_RF__D1, CT_RF__D2, CT_RF__R1[7:3], CT_RF__R1[2:0], CT_RF__R2[7:3], CT_RF__R2[2:0], CT_RF__RA, CT_RF__MA, CT_RF__RB, CT_RF__MB, pcs_i, CT_RF__PCSE, pca_i, CT_RF__PCAE, ISC_i, CT_RF__SCSS, CT_RF__SCSE, sca_i, CT_RF__SCAE, CT_RF__SCAE, {{23{1'b0}}, FL[14], fl_i}, CT_RF__FLS, 4'b0001, pc_read, R_A, R_B, PCS, PCA, SCS, SCA, FL
  or or_21 (or_21_out[0], CT_RF__PCH, CT_RF__PCJ);
  or or_22 (or_21_out[1], CT_RF__PCH, and_69_out);
  add_4c32 add_4c32_2 (.a(PCS), .b(4'b0100), .s(add_4c32_2_s));  // open: c
  Register #(.Bits(37)) BTB_F (
    .D({BTB_packet[36:3], BTB_JP, BTB_packet[1:0]}), .C(C_dt), .en(CT_BUS__IAR), .Q(BTB_fetch));
  Register #(.Bits(32)) I_A__R (.D(PCS), .C(C_dt), .en(CT_BUS__IAR), .Q(I_A__R_q));
  Register #(.Bits(32)) I_D__R (.D({multiplexer_5_out, I_D__bus[23:0]}), .C(C_dt), .en(dc_e), .Q(I_D__R_q));
  Register #(.Bits(37)) BTB_D (.D(BTB_fetch), .C(C_dt), .en(dc_e), .Q(BTB_D_q));
  and and_73 (MB_LDB__LD, LDB_M__V, MEM_LD, not_17_out);
  and and_74 (MB_STB__LD, multiplexer_6_out, MEM_LD);
  Register register_11 (.D(multiplexer_6_out), .C(C_dt), .en(MEM_LD), .Q(MEM_TYPE__ST));
  Register register_12 (.D(LDB_M__EP), .C(C_dt), .en(MEM_LD), .Q(MEM_EP));
  Register #(.Bits(4)) register_13 (.D(LDB_M__ID), .C(C_dt), .en(MEM_LD), .Q(MEM_INST));
  Register #(.Bits(32)) register_14 (.D(multiplexer_8_out), .C(C_dt), .en(MEM_LD), .Q(register_14_q));
  Register #(.Bits(2)) register_15 (.D(multiplexer_9_out), .C(C_dt), .en(MEM_LD), .Q(register_15_q));
  Register #(.Bits(32)) register_16 (.D(STB_M__D), .C(C_dt), .en(MEM_LD), .Q(register_16_q));
  not not_18 (not_18_out, MEM_LD__CLR);
  RS_FF rs_ff_6 (.S(and_62_out), .C(C_dt), .R(and_70_out), .Q(rs_ff_6_q), .nQ(rs_ff_6_nq));
  Register #(.Bits(32)) register_17 (.D(D_D__bus), .C(C_dt), .en(MEM_AC), .Q(MEM_LD__D));
  Register #(.Bits(4)) register_18 (.D(MEM_INST), .C(C_dt), .en(MEM_AC), .Q(MEM_LD__INST));
  Register register_19 (.D(MEM_EP), .C(C_dt), .en(MEM_AC), .Q(MEM_LD__EP));
  and and_75 (and_75_out, byte_D0_iv[7], byte_D0_iv[6], byte_D0_iv[5], byte_D0_iv[4]);
  and and_76 (and_76_out, byte_D0_iv[7], byte_D0_iv[6], byte_D0_iv[5], byte_D0[4], byte_D0_iv[3]);
  assign {CT_RF__RA, CT_RF__MA} = or_25_out ? byte_D1 : 8'bz;  // Driver driver_26
  assign {CT_RF__RB, CT_RF__MB} = or_25_out ? byte_D2 : 8'bz;  // Driver driver_27
  assign CT_ALU__LD = or_25_out ? CT_DISP : 1'bz;  // Driver driver_28
  assign CT_ALU__CT = or_25_out ? {1'b0, and_40_out[7:0]} : 9'bz;  // Driver driver_29
  assign CT_ALU__M = or_25_out ? and_40_out[9] : 1'bz;  // Driver driver_30
  assign CT_FU__INST = or_25_out ? inst_DP : 4'bz;  // Driver driver_31
  assign CT_FU__EPOCH = or_25_out ? epoch_DP : 1'bz;  // Driver driver_32
  assign CT_FU__WR = or_25_out ? byte_D1 : 8'bz;  // Driver driver_33
  assign CT_ALU__WD = or_25_out ? nor_2_out : 1'bz;  // Driver driver_34
  assign CT_ALU__WF = or_25_out ? 1'b1 : 1'bz;  // Driver driver_35
  assign {CT_RF__RA, CT_RF__MA} = or_20_out ? byte_D2 : 8'bz;  // Driver driver_36
  assign CT_DIR__LD = or_20_out ? CT_DISP : 1'bz;  // Driver driver_37
  assign CT_DIR__M = or_20_out ? and_64_out : 1'bz;  // Driver driver_38
  assign CT_DIR__MS = or_20_out ? byte_D0[0] : 1'bz;  // Driver driver_39
  assign CT_FU__INST = or_20_out ? inst_DP : 4'bz;  // Driver driver_40
  assign CT_FU__EPOCH = or_20_out ? epoch_DP : 1'bz;  // Driver driver_41
  assign CT_FU__WR = or_20_out ? byte_D1 : 8'bz;  // Driver driver_42
  assign CT_RF__SCSS = and_65_out ? 1'b1 : 1'bz;  // Driver driver_43
  assign {CT_RF__RB, CT_RF__MB} = and_65_out ? 8'hf0 : 8'bz;  // Driver driver_44
  assign {CT_RF__RA, CT_RF__MA} = and_71_out ? byte_D1 : 8'bz;  // Driver driver_45
  assign CT_FU__WR = and_72_out ? byte_D1 : 8'bz;  // Driver driver_46
  assign CT_MB__LD = and_65_out ? CT_DISP : 1'bz;  // Driver driver_47
  assign CT_MB__ST = and_71_out ? 1'b1 : 1'bz;  // Driver driver_48
  assign CT_SP__MOF = and_71_out ? {1'b1, or_18_out[1], byte_D1[1]} : 3'bz;  // Driver driver_49
  assign CT_MB__OFFM = and_65_out ? 1'b1 : 1'bz;  // Driver driver_50
  assign CT_RF__SCSE = and_65_out ? 1'b1 : 1'bz;  // Driver driver_51
  assign CT_RF__SCN = and_65_out ? {nor_3_out, byte_D1[1]} : 3'bz;  // Driver driver_52
  assign CT_RF__SCD = and_71_out ? 1'b1 : 1'bz;  // Driver driver_53
  assign CT_FU__INST = and_65_out ? inst_DP : 4'bz;  // Driver driver_54
  assign CT_FU__EPOCH = and_65_out ? epoch_DP : 1'bz;  // Driver driver_55
  assign CT_RF__SCSRE = and_65_out ? 1'b1 : 1'bz;  // Driver driver_56
  assign CT_FU__EPOCH = or_19_out ? epoch_DP : 1'bz;  // Driver driver_57
  assign CT_FU__INST = or_19_out ? inst_DP : 4'bz;  // Driver driver_58
  assign {CT_RF__RB, CT_RF__MB} = or_19_out ? {byte_D0[4:0], 3'b000} : 8'bz;  // Driver driver_59
  assign {CT_RF__RA, CT_RF__MA} = and_60_out ? byte_D1 : 8'bz;  // Driver driver_60
  assign CT_FU__WR = and_59_out ? byte_D1 : 8'bz;  // Driver driver_61
  assign CT_MB__LD = or_19_out ? CT_DISP : 1'bz;  // Driver driver_62
  assign CT_MB__ST = and_60_out ? 1'b1 : 1'bz;  // Driver driver_63
  or or_23 (CT_RF__PCAE, com1, com2);
  Multiplexer #(.Selector_Bits(2), .Bits(32)) multiplexer_10 (
    .sel(or_21_out), .in_0(add_4c32_2_s), .in_1(multiplexer_7_out), .in_2(BTB_packet[36:5]),
    .in_3(add_4c32_1_s), .out(pcs_i));
  assign I_A__bus = CT_BUS__IAG ? I_A__R_q : 32'bz;  // Driver driver_64
  D_FF #(.Bits(32)) d_ff_5 (.D(I_D__R_q), .C(C_ct), .Q({byte_I0, byte_I1, byte_I2, byte_I3}));  // open: nQ
  D_FF #(.Bits(37)) d_ff_6 (.D(BTB_D_q), .C(C_ct), .Q(BTB_pack__iss));  // open: nQ
  assign D_A__bus = MEM_RD ? register_14_q : 32'bz;  // Driver driver_65
  assign D_MD = MEM_RD ? register_15_q : 2'bz;  // Driver driver_66
  assign D_D__bus = D_ST ? register_16_q : 32'bz;  // Driver driver_67
  and and_77 (MEM_LD__RD, not_18_out, rs_ff_6_q);
  or or_24 (MEM_BF__free, rs_ff_6_nq, MEM_LD__RD, MEM_LD__CLR);
  PullDown #(.Bits(16)) pulldown_13 (.out(V1_inst));
  PullDown #(.Bits(16)) pulldown_14 (.out(V2_inst));
  PullDown pulldown_15 (.out(CT_RF__SCSRE));
  and and_78 (D_LD, ~MEM_TYPE__ST, MEM_RD);  // And
  and and_79 (D_ST, MEM_RD, MEM_TYPE__ST);
  or or_25 (or_25_out, and_75_out, and_68_out, and_76_out);
  BitExtender #(.inputBits(1), .outputBits(8)) bitextender_2 (.in(byte_D0[3]), .out(bitextender_2_out));
  assign xor_3_out = FL[7:0] ^ bitextender_2_out;  // XOr xor_3, 8 bits wide
  and and_80 (and_80_out, com1, CT_SC__W1);
  and and_81 (and_81_out, com2, CT_SC__W2);
  and and_82 (and_82_out, byte_D2[7], CT_DIR__MS);
  assign CT_RF__SCSE = clr ? 1'b1 : 1'bz;  // Driver driver_68
  assign CT_RF__SCSS = clr ? 1'b1 : 1'bz;  // Driver driver_69
  Multiplexer multiplexer_11 (.sel(and_92_out[2]), .in_0(nand_1_out[2]), .in_1(1'b1), .out(multiplexer_11_out));
  not not_19 (not_19_out[0], register_20_q[0]);
  xor xor_4 (not_19_out[1], register_20_q[0], register_20_q[1]);
  xor xor_5 (not_19_out[2], register_20_q[1], register_20_q[2]);
  Multiplexer #(.Bits(32)) multiplexer_12 (
    .sel(CT_ALU__M), .in_0(R_B), .in_1({{16{1'b0}}, byte_D2, byte_D3}), .out(multiplexer_12_out));
  BitExtender #(.inputBits(1)) bitextender_3 (.in(and_82_out), .out(bitextender_3_out));
  and and_83 (and_83_out, byte_D0_iv[4], byte_D0[5], byte_D0[6], byte_D0_iv[7]);
  Multiplexer #(.Selector_Bits(3)) multiplexer_13 (
    .sel(byte_D0[2:0]), .in_0(xor_3_out[0]), .in_1(xor_3_out[1]), .in_2(xor_3_out[2]), .in_3(xor_3_out[3]),
    .in_4(xor_3_out[4]), .in_5(xor_3_out[5]), .in_6(xor_3_out[6]), .in_7(xor_3_out[7]),
    .out(multiplexer_13_out));
  or or_26 (CT_RF__SCAE, and_80_out, and_81_out);
  and and_84 (and_84_out, multiplexer_11_out, CT_ALU__LD);
  Register register_20 (.D(and_84_out), .C(C_ct), .en(or_27_out), .Q(register_20_q[2]));
  not not_20 (not_20_out, multiplexer_11_out);
  or or_27 (or_27_out, not_20_out, multiplexer_14_out[2]);
  Multiplexer #(.Bits(3)) multiplexer_14 (
    .sel(or_28_out), .in_0(not_19_out), .in_1(and_92_out), .out(multiplexer_14_out));
  or or_28 (or_28_out, and_92_out[0], and_92_out[1], and_92_out[2]);
  Register #(.Bits(4)) register_21 (.D(CT_FU__INST), .C(C_ct), .en(multiplexer_14_out[2]), .Q(register_21_q));
  Register register_22 (.D(CT_FU__EPOCH), .C(C_ct), .en(multiplexer_14_out[2]), .Q(register_22_q));
  Register register_23 (.D(CT_ALU__WD), .C(C_ct), .en(multiplexer_14_out[2]), .Q(register_23_q));
  Register register_24 (.D(CT_ALU__WF), .C(C_ct), .en(multiplexer_14_out[2]), .Q(register_24_q));
  Register #(.Bits(32)) register_25 (.D(R_A), .C(C_dt), .en(multiplexer_14_out[2]), .Q(register_25_q));
  Register #(.Bits(32)) register_26 (.D(multiplexer_12_out), .C(C_dt), .en(multiplexer_14_out[2]), .Q(register_26_q));
  Register #(.Bits(8)) register_27 (.D(FL[7:0]), .C(C_dt), .en(multiplexer_14_out[2]), .Q(register_27_q));
  Register #(.Bits(9)) register_28 (.D(CT_ALU__CT), .C(C_ct), .en(multiplexer_14_out[2]), .Q(register_28_q));
  Register #(.Bits(8)) register_29 (.D(CT_FU__WR), .C(C_ct), .en(multiplexer_14_out[2]), .Q(register_29_q));
  or or_29 (or_29_out, CT_FU__WR[0], CT_FU__WR[2]);
  not not_21 (not_21_out, CT_FU__WR[1]);
  and and_85 (and_85_out, byte_D0_iv[0], byte_D0_iv[1], byte_D0_iv[2], byte_D0_iv[3], byte_D0[4], byte_D0[5], byte_D0[6], byte_D0_iv[7]);
  and and_86 (and_86_out, byte_D0[0], byte_D0_iv[1], byte_D0_iv[2], byte_D0_iv[3], byte_D0[4], byte_D0[5], byte_D0[6], byte_D0_iv[7]);
  and and_87 (and_87_out, byte_D0[0], byte_D0[1], byte_D0_iv[2], byte_D0_iv[3], byte_D0[4], byte_D0[5], byte_D0[6], byte_D0_iv[7]);
  and and_88 (and_88_out, byte_D0[0], byte_D0_iv[1], byte_D0[2], byte_D0[3], byte_D0[4], byte_D0_iv[5], byte_D0_iv[6], byte_D0_iv[7]);
  Multiplexer multiplexer_15 (
    .sel(and_92_out[1]), .in_0(nand_1_out[1]), .in_1(nand_1_out[2]), .out(multiplexer_15_out));
  Multiplexer multiplexer_16 (
    .sel(register_20_q[2]), .in_0(CT_ALU__LD), .in_1(register_20_q[2]), .out(multiplexer_16_out));
  Multiplexer #(.Bits(4)) multiplexer_17 (
    .sel(register_20_q[2]), .in_0(CT_FU__INST), .in_1(register_21_q), .out(multiplexer_17_out));
  inst_comp inst_comp_4 (
    .A_id(register_21_q), .A_ep(register_22_q), .B_id(clr_id), .B_ep(clr_ep), .A_old(inst_comp_4_a_old));
  Multiplexer multiplexer_18 (
    .sel(register_20_q[2]), .in_0(CT_FU__EPOCH), .in_1(register_22_q), .out(multiplexer_18_out));
  Multiplexer multiplexer_19 (
    .sel(register_20_q[2]), .in_0(CT_ALU__WD), .in_1(register_23_q), .out(multiplexer_19_out));
  Multiplexer multiplexer_20 (
    .sel(register_20_q[2]), .in_0(CT_ALU__WF), .in_1(register_24_q), .out(multiplexer_20_out));
  Multiplexer #(.Bits(32)) multiplexer_21 (
    .sel(register_20_q[2]), .in_0(R_A), .in_1(register_25_q), .out(multiplexer_21_out));
  Multiplexer #(.Bits(32)) multiplexer_22 (
    .sel(register_20_q[2]), .in_0(multiplexer_12_out), .in_1(register_26_q), .out(multiplexer_22_out));
  Multiplexer #(.Bits(8)) multiplexer_23 (
    .sel(register_20_q[2]), .in_0(FL[7:0]), .in_1(register_27_q), .out(multiplexer_23_out));
  Multiplexer #(.Bits(9)) multiplexer_24 (
    .sel(register_20_q[2]), .in_0(CT_ALU__CT), .in_1(register_28_q), .out(multiplexer_24_out));
  Multiplexer #(.Bits(8)) multiplexer_25 (
    .sel(register_20_q[2]), .in_0(CT_FU__WR), .in_1(register_29_q), .out(multiplexer_25_out));
  Multiplexer multiplexer_26 (.sel(and_96_out[2]), .in_0(nand_4_out[2]), .in_1(1'b1), .out(multiplexer_26_out));
  not not_22 (not_22_out[0], register_44_q[0]);
  xor xor_6 (not_22_out[1], register_44_q[0], register_44_q[1]);
  xor xor_7 (not_22_out[2], register_44_q[1], register_44_q[2]);
  Multiplexer #(.Bits(32)) multiplexer_27 (
    .sel(CT_DIR__M), .in_0(R_A), .in_1({bitextender_3_out, byte_D2, byte_D3}), .out(multiplexer_27_out));
  Multiplexer #(.Bits(32)) multiplexer_28 (.sel(CT_INTM), .in_0(R_A), .in_1(int_pc), .out(multiplexer_28_out));
  add_4c32 add_4c32_3 (.a(pc_read), .b(4'b0100), .s(add_4c32_3_s));  // open: c
  BitExtender #(.inputBits(3)) bitextender_4 (.in(CT_SP__MOF), .out(bitextender_4_out));
  and and_89 (and_89_out[0], or_29_out, not_21_out);
  and and_90 (and_90_out, multiplexer_15_out, multiplexer_16_out);
  not not_23 (not_23_out, multiplexer_15_out);
  or or_30 (or_30_out, not_23_out, multiplexer_14_out[1]);
  or or_31 (register_20_q[1], register_43_q[1], register_20_q[2]);
  nand nand_1 (nand_1_out[2], inst_comp_4_a_old, register_20_q[2], clr);
  Register #(.Bits(4)) register_30 (.D(multiplexer_17_out), .C(C_ct), .en(multiplexer_14_out[1]), .Q(register_30_q));
  Register register_31 (.D(multiplexer_18_out), .C(C_ct), .en(multiplexer_14_out[1]), .Q(register_31_q));
  Register register_32 (.D(multiplexer_19_out), .C(C_ct), .en(multiplexer_14_out[1]), .Q(register_32_q));
  Register register_33 (.D(multiplexer_20_out), .C(C_ct), .en(multiplexer_14_out[1]), .Q(register_33_q));
  Register #(.Bits(32)) register_34 (.D(multiplexer_21_out), .C(C_dt), .en(multiplexer_14_out[1]), .Q(register_34_q));
  Register #(.Bits(32)) register_35 (.D(multiplexer_22_out), .C(C_dt), .en(multiplexer_14_out[1]), .Q(register_35_q));
  Register #(.Bits(8)) register_36 (.D(multiplexer_23_out), .C(C_dt), .en(multiplexer_14_out[1]), .Q(register_36_q));
  Register #(.Bits(9)) register_37 (.D(multiplexer_24_out), .C(C_ct), .en(multiplexer_14_out[1]), .Q(register_37_q));
  Register #(.Bits(8)) register_38 (.D(multiplexer_25_out), .C(C_ct), .en(multiplexer_14_out[1]), .Q(register_38_q));
  and and_91 (and_91_out, multiplexer_26_out, CT_DIR__LD);
  not not_24 (not_24_out, multiplexer_26_out);
  Register #(.Bits(4)) register_39 (.D(CT_FU__INST), .C(C_ct), .en(multiplexer_42_out[2]), .Q(register_39_q));
  Register register_40 (.D(CT_FU__EPOCH), .C(C_ct), .en(multiplexer_42_out[2]), .Q(register_40_q));
  Register #(.Bits(32)) register_41 (.D(multiplexer_27_out), .C(C_dt), .en(multiplexer_42_out[2]), .Q(register_41_q));
  Register #(.Bits(8)) register_42 (.D(CT_FU__WR), .C(C_ct), .en(multiplexer_42_out[2]), .Q(register_42_q));
  Multiplexer #(.Bits(32)) multiplexer_29 (
    .sel(CT_CALLM), .in_0(multiplexer_28_out), .in_1(add_4c32_3_s), .out(multiplexer_29_out));
  Multiplexer #(.Bits(32)) multiplexer_30 (.sel(CT_INTM), .in_0(R_B), .in_1(ISC), .out(multiplexer_30_out));
  Multiplexer #(.Bits(16)) multiplexer_31 (
    .sel(CT_MB__OFFM), .in_0({byte_D2, byte_D3}), .in_1(bitextender_4_out), .out(multiplexer_31_out));
  assign CT_FU__EPOCH = and_83_out ? epoch_DP : 1'bz;  // Driver driver_70
  assign CT_FU__INST = and_83_out ? inst_DP : 4'bz;  // Driver driver_71
  assign {CT_RF__RA, CT_RF__MA} = and_83_out ? byte_D1 : 8'bz;  // Driver driver_72
  assign CT_JPU__LD = and_83_out ? CT_DISP : 1'bz;  // Driver driver_73
  assign CT_JPU__JP = and_83_out ? multiplexer_13_out : 1'bz;  // Driver driver_74
  assign JPU_A__ST = and_83_out ? 1'b1 : 1'bz;  // Driver driver_75
  assign CT_FU__EPOCH = and_85_out ? epoch_DP : 1'bz;  // Driver driver_76
  assign CT_FU__INST = and_85_out ? inst_DP : 4'bz;  // Driver driver_77
  assign {CT_RF__RA, CT_RF__MA} = and_85_out ? byte_D1 : 8'bz;  // Driver driver_78
  assign {CT_RF__RB, CT_RF__MB} = and_85_out ? 8'hf0 : 8'bz;  // Driver driver_79
  assign CT_JPU__LD = and_85_out ? 1'b1 : 1'bz;  // Driver driver_80
  assign CT_JPU__JP = and_85_out ? CT_DISP : 1'bz;  // Driver driver_81
  assign JPU_A__ST = and_85_out ? 1'b1 : 1'bz;  // Driver driver_82
  assign CT_MB__LD = and_85_out ? 1'b1 : 1'bz;  // Driver driver_83
  assign CT_MB__ST = and_85_out ? 1'b1 : 1'bz;  // Driver driver_84
  assign CT_CALLM = and_85_out ? 1'b1 : 1'bz;  // Driver driver_85
  assign CT_SP__MOF = and_85_out ? 3'b100 : 3'bz;  // Driver driver_86
  assign CT_MB__OFFM = and_85_out ? 1'b1 : 1'bz;  // Driver driver_87
  assign CT_RF__SCSE = and_85_out ? 1'b1 : 1'bz;  // Driver driver_88
  assign CT_RF__SCSS = and_85_out ? 1'b1 : 1'bz;  // Driver driver_89
  assign CT_RF__SCD = and_85_out ? 1'b1 : 1'bz;  // Driver driver_90
  assign CT_RF__SCN = and_85_out ? 3'b100 : 3'bz;  // Driver driver_91
  assign CT_FU__MF = and_85_out ? 1'b1 : 1'bz;  // Driver driver_92
  assign JPU_CALL = and_85_out ? 1'b1 : 1'bz;  // Driver driver_93
  assign CT_RF__SCSRE = and_85_out ? 1'b1 : 1'bz;  // Driver driver_94
  assign CT_FU__EPOCH = and_86_out ? epoch_DP : 1'bz;  // Driver driver_95
  assign CT_FU__INST = and_86_out ? inst_DP : 4'bz;  // Driver driver_96
  assign {CT_RF__RB, CT_RF__MB} = and_86_out ? 8'hf0 : 8'bz;  // Driver driver_97
  assign CT_FU__WR = and_86_out ? 8'he8 : 8'bz;  // Driver driver_98
  assign CT_MB__LD = and_86_out ? 1'b1 : 1'bz;  // Driver driver_99
  assign CT_MB__OFFM = and_86_out ? 1'b1 : 1'bz;  // Driver driver_100
  assign CT_RF__SCSE = and_86_out ? 1'b1 : 1'bz;  // Driver driver_101
  assign CT_RF__SCSS = and_86_out ? 1'b1 : 1'bz;  // Driver driver_102
  assign CT_RF__SCN = and_86_out ? 3'b100 : 3'bz;  // Driver driver_103
  assign CT_FU__MF = and_86_out ? 1'b1 : 1'bz;  // Driver driver_104
  assign CT_RET__LD = and_86_out ? 1'b1 : 1'bz;  // Driver driver_105
  assign CT_RF__SCSRE = and_86_out ? 1'b1 : 1'bz;  // Driver driver_106
  bus16x2_demux bus16x2_demux_1 (.bus_1(V1_inst), .bus_2(V2_inst), .E(and_87_out), .id(inst_DP));
  assign CT_FU__EPOCH = and_87_out ? epoch_DP : 1'bz;  // Driver driver_107
  assign CT_FU__INST = and_87_out ? inst_DP : 4'bz;  // Driver driver_108
  assign CT_HALT__LD = and_87_out ? 1'b1 : 1'bz;  // Driver driver_109
  bus16x2_demux bus16x2_demux_2 (.bus_1(V1_inst), .bus_2(V2_inst), .E(and_88_out), .id(inst_DP));
  Multiplexer #(.Bits(32)) multiplexer_32 (.sel(CT_ISCM), .in_0(SCS), .in_1(ISC), .out(multiplexer_32_out));
  Register register_43 (.D(and_90_out), .C(C_ct), .en(or_30_out), .Q(register_43_q[1]));
  or or_32 (register_20_q[0], ALU_busy, register_43_q[1], register_20_q[2]);
  assign and_92_out = nand_2_out & register_20_q;  // And and_92, 3 bits wide
  Multiplexer #(.Bits(4)) multiplexer_33 (
    .sel(register_20_q[1]), .in_0(CT_FU__INST), .in_1(register_30_q), .out(multiplexer_33_out));
  inst_comp inst_comp_5 (
    .A_id(register_30_q), .A_ep(register_31_q), .B_id(clr_id), .B_ep(clr_ep), .A_old(inst_comp_5_a_old));
  Multiplexer multiplexer_34 (
    .sel(register_20_q[1]), .in_0(CT_FU__EPOCH), .in_1(register_31_q), .out(multiplexer_34_out));
  Multiplexer multiplexer_35 (
    .sel(register_20_q[1]), .in_0(CT_ALU__WD), .in_1(register_32_q), .out(multiplexer_35_out));
  Multiplexer multiplexer_36 (
    .sel(register_20_q[1]), .in_0(CT_ALU__WF), .in_1(register_33_q), .out(multiplexer_36_out));
  Multiplexer #(.Bits(32)) multiplexer_37 (
    .sel(register_20_q[1]), .in_0(R_A), .in_1(register_34_q), .out(multiplexer_37_out));
  Multiplexer #(.Bits(32)) multiplexer_38 (
    .sel(register_20_q[1]), .in_0(multiplexer_12_out), .in_1(register_35_q), .out(multiplexer_38_out));
  Multiplexer #(.Bits(8)) multiplexer_39 (
    .sel(register_20_q[1]), .in_0(FL[7:0]), .in_1(register_36_q), .out(multiplexer_39_out));
  Multiplexer #(.Bits(9)) multiplexer_40 (
    .sel(register_20_q[1]), .in_0(CT_ALU__CT), .in_1(register_37_q), .out(multiplexer_40_out));
  Multiplexer #(.Bits(8)) multiplexer_41 (
    .sel(register_20_q[1]), .in_0(CT_FU__WR), .in_1(register_38_q), .out(multiplexer_41_out));
  Register register_44 (.D(and_91_out), .C(C_ct), .en(or_33_out), .Q(register_44_q[2]));
  or or_33 (or_33_out, not_24_out, multiplexer_42_out[2]);
  Multiplexer #(.Bits(3)) multiplexer_42 (
    .sel(or_34_out), .in_0(not_22_out), .in_1(and_96_out), .out(multiplexer_42_out));
  or or_34 (or_34_out, and_96_out[0], and_96_out[1], and_96_out[2]);
  Multiplexer #(.Bits(4)) multiplexer_43 (
    .sel(register_44_q[2]), .in_0(CT_FU__INST), .in_1(register_39_q), .out(multiplexer_43_out));
  inst_comp inst_comp_6 (
    .A_id(register_39_q), .A_ep(register_40_q), .B_id(clr_id), .B_ep(clr_ep), .A_old(inst_comp_6_a_old));
  Multiplexer multiplexer_44 (
    .sel(register_44_q[2]), .in_0(CT_FU__EPOCH), .in_1(register_40_q), .out(multiplexer_44_out));
  Multiplexer #(.Bits(32)) multiplexer_45 (
    .sel(register_44_q[2]), .in_0(multiplexer_27_out), .in_1(register_41_q), .out(multiplexer_45_out));
  Multiplexer #(.Bits(8)) multiplexer_46 (
    .sel(register_44_q[2]), .in_0(CT_FU__WR), .in_1(register_42_q), .out(multiplexer_46_out));
  and and_93 (MB_LD, MB_free, CT_MB__LD);
  Register register_45 (.D(CT_MB__LD), .C(C_ct), .en(1'b1), .Q(register_45_q));
  Register #(.Bits(4)) register_46 (.D(CT_FU__INST), .C(C_ct), .en(MB_LD), .Q(MB_INST));
  Register register_47 (.D(CT_FU__EPOCH), .C(C_ct), .en(MB_LD), .Q(MB_ep));
  Register register_48 (.D(CT_MB__ST), .C(C_ct), .en(MB_LD), .Q(MB_type__st));
  Register #(.Bits(32)) register_49 (.D(multiplexer_29_out), .C(C_dt), .en(MB_LD), .Q(MB_data));
  Register #(.Bits(32)) register_50 (.D(multiplexer_30_out), .C(C_dt), .en(MB_LD), .Q(register_50_q));
  Register #(.Bits(16)) register_51 (.D(multiplexer_31_out), .C(C_dt), .en(MB_LD), .Q(register_51_q));
  Register #(.Bits(2)) register_52 (.D({CT_FU__WR[1], and_89_out[0]}), .C(C_ct), .en(MB_LD), .Q(MB_MD));
  Register #(.Bits(8)) register_53 (.D(CT_FU__WR), .C(C_ct), .en(MB_LD), .Q(MB_WR));
  Register register_54 (.D(CT_FU__MF), .C(C_ct), .en(MB_LD), .Q(MB_MF));
  Register #(.Bits(32)) register_55 (.D(pc_read), .C(C_dt), .en(MB_LD), .Q(MB_PC));
  Multiplexer #(.Bits(32)) multiplexer_47 (.sel(and_81_out), .in_0(CT_SC__D1), .in_1(CT_SC__D2), .out(sca_i));
  Multiplexer multiplexer_48 (
    .sel(and_92_out[0]), .in_0(nand_1_out[0]), .in_1(nand_1_out[1]), .out(multiplexer_48_out));
  Multiplexer multiplexer_49 (
    .sel(register_20_q[1]), .in_0(CT_ALU__LD), .in_1(register_43_q[1]), .out(multiplexer_49_out));
  and and_94 (and_94_out, multiplexer_48_out, multiplexer_49_out);
  nand nand_2 (nand_2_out[2], ALU_busy, register_43_q[1], register_20_q[2]);
  nand nand_3 (nand_1_out[1], inst_comp_5_a_old, register_43_q[1], clr);
  Register #(.Bits(4)) register_56 (.D(multiplexer_33_out), .C(C_ct), .en(ALU_A_LD), .Q(ALU_A_INST));
  Register register_57 (.D(multiplexer_34_out), .C(C_ct), .en(ALU_A_LD), .Q(register_57_q));
  Register #(.Bits(32)) register_58 (.D(multiplexer_37_out), .C(C_dt), .en(ALU_A_LD), .Q(ALU_A_A));
  Register #(.Bits(32)) register_59 (.D(multiplexer_38_out), .C(C_dt), .en(ALU_A_LD), .Q(ALU_A_B));
  Register #(.Bits(8)) register_60 (.D(multiplexer_39_out), .C(C_dt), .en(ALU_A_LD), .Q(ALU_A_FI));
  Register #(.Bits(9)) register_61 (.D(multiplexer_40_out), .C(C_ct), .en(ALU_A_LD), .Q(ALU_A_CT));
  Register #(.Bits(8)) register_62 (.D(multiplexer_41_out), .C(C_ct), .en(ALU_A_LD), .Q({ALU_A_WR, ALU_A_RM}));
  Multiplexer multiplexer_50 (
    .sel(and_96_out[1]), .in_0(nand_4_out[1]), .in_1(nand_4_out[2]), .out(multiplexer_50_out));
  Multiplexer multiplexer_51 (
    .sel(register_44_q[2]), .in_0(CT_DIR__LD), .in_1(register_44_q[2]), .out(multiplexer_51_out));
  and and_95 (and_95_out, multiplexer_50_out, multiplexer_51_out);
  not not_25 (not_25_out, multiplexer_50_out);
  nand nand_4 (nand_4_out[2], inst_comp_6_a_old, register_44_q[2], clr);
  Register #(.Bits(4)) register_63 (.D(multiplexer_43_out), .C(C_ct), .en(multiplexer_42_out[1]), .Q(register_63_q));
  Register register_64 (.D(multiplexer_44_out), .C(C_ct), .en(multiplexer_42_out[1]), .Q(register_64_q));
  Register #(.Bits(32)) register_65 (.D(multiplexer_45_out), .C(C_dt), .en(multiplexer_42_out[1]), .Q(register_65_q));
  Register #(.Bits(8)) register_66 (.D(multiplexer_46_out), .C(C_ct), .en(multiplexer_42_out[1]), .Q(register_66_q));
  addsub_4c32 addsub_4c32_1 (
    .a(multiplexer_32_out), .b({1'b0, CT_RF__SCN}), .sub(CT_RF__SCD), .s(addsub_4c32_1_s));  // open: c
  nand nand_5 (nand_2_out[1], ALU_busy, register_43_q[1]);
  Register register_67 (.D(and_95_out), .C(C_ct), .en(or_35_out), .Q(register_67_q[1]));
  or or_35 (or_35_out, not_25_out, multiplexer_42_out[1]);
  or or_36 (register_44_q[1], register_67_q[1], register_44_q[2]);
  assign and_96_out = nand_8_out & register_44_q;  // And and_96, 3 bits wide
  Multiplexer #(.Bits(4)) multiplexer_52 (
    .sel(register_44_q[1]), .in_0(CT_FU__INST), .in_1(register_63_q), .out(multiplexer_52_out));
  inst_comp inst_comp_7 (
    .A_id(register_63_q), .A_ep(register_64_q), .B_id(clr_id), .B_ep(clr_ep), .A_old(inst_comp_7_a_old));
  Multiplexer multiplexer_53 (
    .sel(register_44_q[1]), .in_0(CT_FU__EPOCH), .in_1(register_64_q), .out(multiplexer_53_out));
  Multiplexer #(.Bits(32)) multiplexer_54 (
    .sel(register_44_q[1]), .in_0(multiplexer_27_out), .in_1(register_65_q), .out(multiplexer_54_out));
  Multiplexer #(.Bits(8)) multiplexer_55 (
    .sel(register_44_q[1]), .in_0(CT_FU__WR), .in_1(register_66_q), .out(multiplexer_55_out));
  and and_97 (MB_MFE, MB_MF, register_45_q);
  and and_98 (MB_st__e, register_45_q, MB_type__st);
  and and_99 (MB_ld__e, register_45_q, ~MB_type__st);  // And
  add_s16c32 add_s16c32_1 (.a(register_50_q), .b(register_51_q), .s(MB_addr));  // open: c
  Multiplexer #(.Bits(32)) multiplexer_56 (.sel(clr), .in_0(addsub_4c32_1_s), .in_1(CT_SC__FD), .out(ISC_i));
  not not_26 (nand_2_out[0], ALU_busy);
  nand nand_6 (nand_1_out[0], or_39_out, ALU_busy, clr);
  inst_comp inst_comp_8 (.A_id(ALU_A_INST), .A_ep(register_57_q), .B_id(clr_id), .B_ep(clr_ep), .A_old(ALU_A_CMP));
  Multiplexer multiplexer_57 (
    .sel(and_96_out[0]), .in_0(nand_4_out[0]), .in_1(nand_4_out[1]), .out(multiplexer_57_out));
  Multiplexer multiplexer_58 (
    .sel(register_44_q[1]), .in_0(CT_DIR__LD), .in_1(register_67_q[1]), .out(multiplexer_58_out));
  and and_100 (and_100_out, multiplexer_57_out, multiplexer_58_out);
  or or_37 (register_44_q[0], DIR_busy, register_67_q[1], register_44_q[2]);
  nand nand_7 (nand_4_out[1], inst_comp_7_a_old, register_67_q[1], clr);
  Register #(.Bits(4)) register_68 (.D(multiplexer_52_out), .C(C_ct), .en(DIR_LD), .Q(DIR_INST));
  Register register_69 (.D(multiplexer_53_out), .C(C_ct), .en(DIR_LD), .Q(register_69_q));
  Register #(.Bits(32)) register_70 (.D(multiplexer_54_out), .C(C_dt), .en(DIR_LD), .Q(DIR));
  Register #(.Bits(8)) register_71 (.D(multiplexer_55_out), .C(C_ct), .en(DIR_LD), .Q(DIR_WR));
  Register #(.Bits(4)) register_72 (.D(multiplexer_33_out), .C(C_ct), .en(ALU_B_LD), .Q(ALU_B_INST));
  Register register_73 (.D(multiplexer_34_out), .C(C_ct), .en(ALU_B_LD), .Q(register_73_q));
  Register #(.Bits(32)) register_74 (.D(multiplexer_37_out), .C(C_dt), .en(ALU_B_LD), .Q(ALU_B_A));
  Register #(.Bits(32)) register_75 (.D(multiplexer_38_out), .C(C_dt), .en(ALU_B_LD), .Q(ALU_B_B));
  Register #(.Bits(8)) register_76 (.D(multiplexer_39_out), .C(C_dt), .en(ALU_B_LD), .Q(ALU_B_FI));
  Register #(.Bits(9)) register_77 (.D(multiplexer_40_out), .C(C_ct), .en(ALU_B_LD), .Q(ALU_B_CT));
  Register #(.Bits(8)) register_78 (.D(multiplexer_41_out), .C(C_ct), .en(ALU_B_LD), .Q({ALU_B_WR, ALU_B_RM}));
  nand nand_8 (nand_8_out[2], DIR_busy, register_67_q[1], register_44_q[2]);
  and and_101 (LDB_forward, MB_ld__e, LDB_ldV);
  or or_38 (or_38_out, MEM_LD__RD, LDB_forward);
  and and_102 (and_102_out[0], ALU_A_LD, multiplexer_35_out);
  BitExtender #(.inputBits(1), .outputBits(2)) bitextender_5 (.in(ALU_A_CLR), .out(bitextender_5_out));
  and and_103 (and_102_out[1], ALU_A_LD, multiplexer_36_out);
  and and_104 (and_104_out[0], ALU_B_LD, multiplexer_35_out);
  BitExtender #(.inputBits(1), .outputBits(2)) bitextender_6 (.in(ALU_B_CLR), .out(bitextender_6_out));
  and and_105 (and_104_out[1], ALU_B_LD, multiplexer_36_out);
  or or_39 (or_39_out, ALU_A_CMP, ALU_B_CMP);
  nand nand_9 (nand_8_out[1], DIR_busy, register_67_q[1]);
  not not_27 (nand_8_out[0], DIR_busy);
  inst_comp inst_comp_9 (
    .A_id(DIR_INST), .A_ep(register_69_q), .B_id(clr_id), .B_ep(clr_ep), .A_old(inst_comp_9_a_old));
  and and_106 (and_106_out, CT_ISS__OSTB, ~clr);  // And
  Multiplexer #(.Bits(32)) multiplexer_59 (
    .sel(LDB_forward), .in_0(MEM_LD__D), .in_1(LDB_ldD), .out(multiplexer_59_out));
  Multiplexer #(.Bits(4)) multiplexer_60 (
    .sel(LDB_forward), .in_0(MEM_LD__INST), .in_1(MB_INST), .out(multiplexer_60_out));
  and and_107 (and_107_out, CT_ISS__OLDB, ~clr);  // And
  and and_108 (and_108_out, ~and_102_out[0], ALU_A_STD);  // And
  and and_109 (and_109_out, ~and_102_out[1], ALU_A_STF);  // And
  and and_110 (and_110_out, ~and_104_out[0], ALU_B_STD);  // And
  and and_111 (and_111_out, ~and_104_out[1], ALU_B_STF);  // And
  inst_comp inst_comp_10 (.A_id(ALU_B_INST), .A_ep(register_73_q), .B_id(clr_id), .B_ep(clr_ep), .A_old(ALU_B_CMP));
  nand nand_10 (nand_4_out[0], inst_comp_9_a_old, DIR_busy, clr);
  and and_112 (and_112_out, byte_I0[3], byte_I0[0]);
  and and_113 (and_113_out, byte_I0[2], byte_I0[0]);
  and and_114 (and_114_out, byte_I0_iv[3], byte_I0_iv[2], byte_I0[1], byte_I0_iv[0]);
  and and_115 (and_115_out, byte_I0_iv[2], byte_I0_iv[0]);
  and and_116 (and_116_out, byte_I0[2], byte_I0[0]);
  and and_117 (and_117_out, byte_I0[1], byte_I0[2], byte_I0[4]);
  and and_118 (and_118_out, byte_I0[3], byte_I0[4]);
  D_FF #(.Bits(2)) d_ff_7 (.D(and_102_out), .C(C_ct), .Q(d_ff_7_q));  // open: nQ
  assign and_119_out = d_ff_7_q & ~bitextender_5_out;  // And and_119, 2 bits wide
  RS_FF rs_ff_7 (.S(and_102_out[0]), .C(C_ct), .R(and_108_out), .nQ(rs_ff_7_nq));  // open: Q
  RS_FF rs_ff_8 (.S(and_102_out[1]), .C(C_ct), .R(and_109_out), .nQ(rs_ff_8_nq));  // open: Q
  D_FF #(.Bits(2)) d_ff_8 (.D(and_104_out), .C(C_ct), .Q(d_ff_8_q));  // open: nQ
  assign and_120_out = d_ff_8_q & ~bitextender_6_out;  // And and_120, 2 bits wide
  RS_FF rs_ff_9 (.S(and_104_out[0]), .C(C_ct), .R(and_110_out), .nQ(rs_ff_9_nq));  // open: Q
  RS_FF rs_ff_10 (.S(and_104_out[1]), .C(C_ct), .R(and_111_out), .nQ(rs_ff_10_nq));  // open: Q
  and and_121 (and_121_out, ~and_100_out, DIR_ST);  // And
  and and_122 (DIR_CLR, clr, inst_comp_9_a_old);
  store_buffer_debug store_buffer_debug_1 (
    .C(C_dt), .LD(MB_STB__LD), .W_d(MB_st__e), .inst_W(MB_INST), .D(MB_data), .A(MB_addr), .MD(MB_MD),
    .W_id(and_106_out), .epoch(epoch_IS), .inst(inst_IS), .com1(com1), .com2(com2), .com1_id(com1_inst),
    .com2_id(com2_inst), .ld_ep(MB_ep), .ld_id(MB_INST), .ld_addr(MB_addr), .clr(clr), .clr_ep(clr_ep),
    .clr_id(clr_id), .full(store_buffer_debug_1_full), .V(STB_M__V), .D_O(STB_M__D), .A_O(STB_M__A),
    .MD_O(STB_M__MD), .id_O(STB_M__ID), .ep_O(STB_M__EP), .ld_V(LDB_ldV), .ld_D(LDB_ldD));
  load_buffer_debug load_buffer_debug_1 (
    .C(C_dt), .LD(MB_LDB__LD), .LDB(FU_D__V[3]), .W_d(or_38_out), .inst_WD(multiplexer_60_out),
    .D(multiplexer_59_out), .W_a(MB_ld__e), .WC_a(LDB_forward), .inst_WA(MB_INST), .A(MB_addr), .MD(MB_MD),
    .MF(MB_MF), .WR(MB_WR), .PC(MB_PC), .W_id(and_107_out), .epoch(epoch_IS), .inst(inst_IS), .com1(com1),
    .com2(com2), .com1_id(com1_inst), .com2_id(com2_inst), .st(MB_st__e), .st_ep(MB_ep), .st_id(MB_INST),
    .st_addr(MB_addr), .st_data(MB_data), .clr(clr), .clr_ep(clr_ep), .clr_id(clr_id),
    .full(load_buffer_debug_1_full), .V(load_buffer_debug_1_v), .D_O(LDB_B__D),
    .id_O(load_buffer_debug_1_id_o), .WR_O(load_buffer_debug_1_wr_o), .MF_O(load_buffer_debug_1_mf_o),
    .M_V(LDB_M__V), .M_A(LDB_M__A), .M_MD(LDB_M__MD), .M_id(LDB_M__ID), .M_ep(LDB_M__EP), .fl(Fl_MEM),
    .fl_ep(FL_MEM__EP), .fl_id(FL_MEM__ID), .fl_PC(MEM_FPC));
  and and_123 (and_123_out, byte_I0_iv[7], byte_I0_iv[6], byte_I0[5]);
  and and_124 (and_124_out, byte_I0_iv[7], byte_I0[6], byte_I0_iv[5]);
  D_FF #(.Bits(2)) d_ff_9 (.D(and_119_out), .C(C_ct), .Q(d_ff_9_q));  // open: nQ
  and and_125 (ALU_A_UUD, rs_ff_7_nq, ALU_A_V);
  and and_126 (ALU_A_UUF, rs_ff_8_nq, ALU_A_V);
  D_FF #(.Bits(2)) d_ff_10 (.D(and_120_out), .C(C_ct), .Q(d_ff_10_q));  // open: nQ
  and and_127 (ALU_B_UUD, rs_ff_9_nq, ALU_B_V);
  and and_128 (ALU_B_UUF, rs_ff_10_nq, ALU_B_V);
  or or_40 (or_40_out, ALU_A_CLR, and_150_out);
  or or_41 (or_41_out, ALU_B_CLR, and_151_out);
  // alu_32 alu_32_1: pin names not known; wires that end beside it: ALU_A_A, ALU_A_B, ALU_A_FI, ALU_A_CT, ALU_A_RM, alu_32_1_p6, alu_32_1_p6, alu_32_1_p8, alu_32_1_p9, alu_32_1_p9, alu_32_1_p11, alu_32_1_p12, alu_32_1_p12, alu_32_1_p14, ALU_A_R, ALU_A_F
  alu_32 alu_32_2 (
    .A(ALU_B_A), .B(ALU_B_B), .F_I(ALU_B_FI), .CT(ALU_B_CT), .RM(ALU_B_RM), .E_A(alu_32_1_p8),
    .E_B(alu_32_1_p11), .E(alu_32_1_p14), .R_O(ALU_B_R), .F_O(ALU_B_F));
  RS_FF rs_ff_11 (.S(and_100_out), .C(C_ct), .R(and_121_out), .nQ(rs_ff_11_nq));  // open: Q
  D_FF V (.D(DIR_LD), .C(C_ct), .Q(V_q));  // open: nQ
  bus16x2_demux bus16x2_demux_3 (.bus_1(V1_inst), .bus_2(V2_inst), .E(DIR_V), .id(DIR_INST));
  and and_129 (and_129_out, byte_I0[4], byte_I0[3], byte_I0_iv[1], byte_I0_iv[2], byte_I0_iv[5], byte_I0_iv[6], byte_I0_iv[7]);
  or or_42 (or_42_out, and_112_out, and_113_out, and_114_out);
  nor nor_5 (nor_5_out, byte_I0[3], byte_I0[1], and_115_out, and_116_out);
  nor nor_6 (nor_6_out, and_117_out, and_118_out);
  and and_130 (and_130_out, byte_I0_iv[0], byte_I0_iv[1], byte_I0[2], byte_I0[3], byte_I0[4], byte_I0_iv[5], byte_I0_iv[6], byte_I0_iv[7]);
  and and_131 (and_131_out, byte_I0[1], byte_I0_iv[2], byte_I0[3], byte_I0[4], byte_I0_iv[5], byte_I0_iv[6], byte_I0_iv[7]);
  and and_132 (and_132_out, byte_I0_iv[4], undriven_2[5], undriven_2[6], byte_I0_iv[7]);
  and and_133 (and_133_out, com1, CT_FL__W1);
  and and_134 (and_134_out, com2, CT_FL__W2);
  assign {ALU_A_FRE, ALU_A_DRE} = d_ff_9_q & ~bitextender_5_out;  // And and_135, 2 bits wide
  assign {ALU_B_FRE, ALU_B_DRE} = d_ff_10_q & ~bitextender_6_out;  // And and_136, 2 bits wide
  and and_137 (and_137_out, ALU_A_VD, ~or_40_out);  // And
  and and_138 (and_138_out, ALU_A_VF, ~or_40_out);  // And
  and and_139 (and_139_out, ALU_B_VD, ~or_41_out);  // And
  and and_140 (and_140_out, ALU_B_VF, ~or_41_out);  // And
  PullDown #(.Bits(32)) pulldown_16 (.out(alu_32_1_p12));
  PullDown #(.Bits(32)) pulldown_17 (.out(alu_32_1_p14));
  or or_43 (DIR_free, DIR_ST, rs_ff_11_nq);
  and and_141 (DIR_RD, V_q, ~DIR_CLR);  // And
  D_FF d_ff_11 (.D(store_buffer_debug_1_full), .C(C_ct), .Q(STB_busy));  // open: nQ
  D_FF d_ff_12 (.D(load_buffer_debug_1_full), .C(C_ct), .Q(LDB_busy));  // open: nQ
  D_FF #(.Bits(4)) d_ff_13 (.D(load_buffer_debug_1_id_o), .C(C_ct), .Q(LDB_B__INST));  // open: nQ
  D_FF d_ff_14 (.D(load_buffer_debug_1_mf_o), .C(C_ct), .Q(LDB_B__MF));  // open: nQ
  not not_28 (not_28_out, byte_I0[0]);
  and and_142 (and_142_out, byte_I0[1], byte_I0[2], byte_I0[3], byte_I0[4], byte_I0_iv[5], byte_I0_iv[6], byte_I0_iv[7]);
  or or_44 (or_44_out, and_123_out, and_124_out);
  Comparator #(.Bits(3)) comparator_19 (.a(undriven), .b(3'b110), .eq(comparator_19_eq));  // open: gt, lt
  or or_45 (CT_RF__FLS, and_133_out, and_134_out);
  RS_FF rs_ff_12 (.S(ALU_A_DRE), .C(C_ct), .R(ALU_A_DRD), .Q(ALU_A_DRD));  // open: nQ
  RS_FF rs_ff_13 (.S(ALU_A_FRE), .C(C_ct), .R(ALU_A_FRD), .Q(ALU_A_FRD));  // open: nQ
  RS_FF rs_ff_14 (.S(ALU_B_DRE), .C(C_ct), .R(ALU_B_DRD), .Q(ALU_B_DRD));  // open: nQ
  RS_FF rs_ff_15 (.S(ALU_B_FRE), .C(C_ct), .R(ALU_B_FRD), .Q(ALU_B_FRD));  // open: nQ
  RS_FF rs_ff_16 (.S(and_137_out), .C(C_ct), .R(or_40_out), .Q(rs_ff_16_q));  // open: nQ
  RS_FF rs_ff_17 (.S(and_138_out), .C(C_ct), .R(or_40_out), .Q(rs_ff_17_q));  // open: nQ
  RS_FF rs_ff_18 (.S(and_139_out), .C(C_ct), .R(or_41_out), .Q(rs_ff_18_q));  // open: nQ
  RS_FF rs_ff_19 (.S(and_140_out), .C(C_ct), .R(or_41_out), .Q(rs_ff_19_q));  // open: nQ
  D_FF #(.Bits(8)) d_ff_15 (.D(load_buffer_debug_1_wr_o), .C(C_ct), .Q(LDB_B__WR));  // open: nQ
  and and_143 (and_143_out, byte_I0_iv[7], byte_I0_iv[6], byte_I0_iv[5], byte_I0_iv[4]);
  and and_144 (and_144_out, byte_I0_iv[7], byte_I0_iv[6], byte_I0_iv[5], byte_I0[4], byte_I0_iv[3]);
  or or_46 (or_46_out, and_130_out, and_131_out);
  and and_145 (and_145_out, byte_I0[0], byte_I0_iv[1], byte_I0[2], byte_I0[3], byte_I0[4], byte_I0_iv[5], byte_I0_iv[6], byte_I0_iv[7]);
  not not_29 (not_29_out, comparator_19_eq);
  or or_47 (or_47_out, ALU_A_VD, ALU_A_UUD, rs_ff_16_q);
  or or_48 (or_48_out, ALU_A_VF, ALU_A_UUF, rs_ff_17_q);
  or or_49 (or_49_out, ALU_B_VD, ALU_B_UUD, rs_ff_18_q);
  or or_50 (or_50_out, ALU_B_VF, ALU_B_UUF, rs_ff_19_q);
  and and_146 (DIR_LD, and_100_out, DIR_free);
  not not_30 (DIR_busy, DIR_free);
  and and_147 (and_147_out, d_ff_16_q, ~FU_D__V[3]);  // And
  not not_31 (not_31_out, or_42_out);
  and and_148 (and_148_out, and_142_out, byte_I0[0]);
  and and_149 (and_149_out, not_28_out, and_142_out);
  or or_51 (or_51_out, ALU_A_STD, rs_ff_7_nq);
  or or_52 (or_52_out, ALU_A_STF, rs_ff_8_nq);
  or or_53 (or_53_out, ALU_B_STD, rs_ff_9_nq);
  or or_54 (or_54_out, ALU_B_STF, rs_ff_10_nq);
  and and_150 (and_150_out, or_47_out, ~ALU_A_CLR, or_48_out);  // And
  bus16x2_demux bus16x2_demux_4 (.bus_1(V1_inst), .bus_2(V2_inst), .E(and_150_out), .id(ALU_A_INST));
  and and_151 (and_151_out, or_49_out, ~ALU_B_CLR, or_50_out);  // And
  bus16x2_demux bus16x2_demux_5 (.bus_1(V1_inst), .bus_2(V2_inst), .E(and_151_out), .id(ALU_B_INST));
  nor nor_7 (ALU_busy, ALU_A_LRD, ALU_B_LRD);
  or or_55 (ALU_free, ALU_A_LRD, ALU_B_LRD);
  Register #(.Bits(32)) register_79 (.D(ALU_A_R), .C(C_dt), .en(ALU_A_DRE), .Q(ALU_A_T__R));
  Register #(.Bits(8)) register_80 (.D(ALU_A_F), .C(C_dt), .en(ALU_A_FRE), .Q(ALU_A_T__F));
  Register #(.Bits(32)) register_81 (.D(ALU_B_R), .C(C_dt), .en(ALU_B_DRE), .Q(ALU_B_T__R));
  Register #(.Bits(8)) register_82 (.D(ALU_B_F), .C(C_dt), .en(ALU_B_FRE), .Q(ALU_B_T__F));
  and and_152 (and_152_out, ~MB_MF, MB_st__e);  // And
  and and_153 (and_153_out, ~LDB_B__MF, FU_D__V[3]);  // And
  D_FF d_ff_16 (.D(load_buffer_debug_1_v), .C(C_ct), .Q(d_ff_16_q));  // open: nQ
  D_FF d_ff_17 (.D(and_147_out), .C(C_ct), .nQ(d_ff_17_nq));  // open: Q
  and and_154 (LDB_B__RD, d_ff_16_q, d_ff_17_nq);
  or or_56 (or_56_out, and_143_out, and_129_out, and_144_out);
  assign issue = or_56_out ? issue_e : 1'bz;  // Driver driver_110
  assign CT_ISS__URA = or_56_out ? 1'b1 : 1'bz;  // Driver driver_111
  assign CT_ISS__URB = or_56_out ? not_31_out : 1'bz;  // Driver driver_112
  assign CT_ISS__RA = or_56_out ? byte_I1[7:3] : 5'bz;  // Driver driver_113
  assign CT_ISS__RB = or_56_out ? byte_I2[7:3] : 5'bz;  // Driver driver_114
  assign CT_ISS__UFL = or_56_out ? nor_5_out : 1'bz;  // Driver driver_115
  assign CT_ISS__ORC = or_56_out ? nor_6_out : 1'bz;  // Driver driver_116
  assign CT_ISS__RC = or_56_out ? byte_I1[7:3] : 5'bz;  // Driver driver_117
  assign CT_ISS__OFL = or_56_out ? 1'b1 : 1'bz;  // Driver driver_118
  assign CT_ISS__UFU = or_56_out ? 3'b001 : 3'bz;  // Driver driver_119
  assign CT_ISS__URA = and_130_out ? 1'b1 : 1'bz;  // Driver driver_120
  assign CT_ISS__RA = and_130_out ? byte_I2[7:3] : 5'bz;  // Driver driver_121
  assign issue = or_46_out ? issue_e : 1'bz;  // Driver driver_122
  assign CT_ISS__ORC = or_46_out ? 1'b1 : 1'bz;  // Driver driver_123
  assign CT_ISS__RC = or_46_out ? byte_I1[7:3] : 5'bz;  // Driver driver_124
  assign CT_ISS__UFU = or_46_out ? 3'b010 : 3'bz;  // Driver driver_125
  assign issue = and_142_out ? issue_e : 1'bz;  // Driver driver_126
  assign CT_ISS__URB = and_142_out ? 1'b1 : 1'bz;  // Driver driver_127
  assign CT_ISS__RB = and_142_out ? 5'b11110 : 5'bz;  // Driver driver_128
  assign CT_ISS__OSC = and_142_out ? 1'b1 : 1'bz;  // Driver driver_129
  assign CT_ISS__UMM = and_142_out ? 1'b1 : 1'bz;  // Driver driver_130
  assign CT_ISS__UFU = and_142_out ? 3'b011 : 3'bz;  // Driver driver_131
  assign CT_ISS__URA = and_148_out ? 1'b1 : 1'bz;  // Driver driver_132
  assign CT_ISS__RA = and_148_out ? byte_I1[7:3] : 5'bz;  // Driver driver_133
  assign CT_ISS__OSTB = and_148_out ? issue_e : 1'bz;  // Driver driver_134
  assign CT_ISS__ORC = and_149_out ? 1'b1 : 1'bz;  // Driver driver_135
  assign CT_ISS__RC = and_149_out ? byte_I1[7:3] : 5'bz;  // Driver driver_136
  assign CT_ISS__OLDB = and_149_out ? issue_e : 1'bz;  // Driver driver_137
  assign issue = or_44_out ? issue_e : 1'bz;  // Driver driver_138
  assign CT_ISS__URA = or_44_out ? 1'b1 : 1'bz;  // Driver driver_139
  assign CT_ISS__RA = or_44_out ? byte_I0[4:0] : 5'bz;  // Driver driver_140
  assign CT_ISS__UMM = or_44_out ? 1'b1 : 1'bz;  // Driver driver_141
  assign CT_ISS__UFU = or_44_out ? 3'b011 : 3'bz;  // Driver driver_142
  assign CT_ISS__URB = and_124_out ? 1'b1 : 1'bz;  // Driver driver_143
  assign CT_ISS__RB = and_124_out ? byte_I1[7:3] : 5'bz;  // Driver driver_144
  assign CT_ISS__ORC = and_123_out ? 1'b1 : 1'bz;  // Driver driver_145
  assign CT_ISS__RC = and_123_out ? byte_I1[7:3] : 5'bz;  // Driver driver_146
  assign CT_ISS__OLDB = and_123_out ? issue_e : 1'bz;  // Driver driver_147
  assign CT_ISS__OSTB = and_124_out ? issue_e : 1'bz;  // Driver driver_148
  assign issue = and_145_out ? issue_e : 1'bz;  // Driver driver_149
  assign CT_BLOCK = and_145_out ? 1'b1 : 1'bz;  // Driver driver_150
  assign CT_UBTB = and_132_out ? issue_e : 1'bz;  // Driver driver_151
  assign issue = and_132_out ? issue_e : 1'bz;  // Driver driver_152
  assign CT_ISS__URA = and_132_out ? 1'b1 : 1'bz;  // Driver driver_153
  assign CT_ISS__RA = and_132_out ? byte_I1[7:3] : 5'bz;  // Driver driver_154
  assign CT_ISS__UFL = and_132_out ? not_29_out : 1'bz;  // Driver driver_155
  assign CT_ISS__UFU = and_132_out ? 3'b111 : 3'bz;  // Driver driver_156
  DipSwitch dipswitch_15 (.out(MB_busy));
  Multiplexer #(.Bits(8)) multiplexer_61 (.sel(and_134_out), .in_0(CT_FL__D1), .in_1(CT_FL__D2), .out(fl_i));
  and and_155 (ALU_A_LD, and_94_out, or_52_out, or_51_out);
  and and_156 (ALU_A_LRD, or_51_out, or_52_out);
  nand nand_11 (nand_11_out, or_51_out, or_52_out);
  and and_157 (ALU_B_LD, nand_11_out, and_94_out, or_54_out, or_53_out);
  and and_158 (ALU_B_LRD, or_53_out, or_54_out);
  and and_159 (and_159_out, ~ALU_A_LD, or_40_out);  // And
  and and_160 (and_160_out, ~ALU_B_LD, or_41_out);  // And
  bus16_demux bus16_demux_1 (.bus(V1_inst), .E(MB_st__e), .id(MB_INST));
  bus16_demux bus16_demux_2 (.bus(V2_inst), .E(and_152_out), .id(MB_INST));
  bus16_demux bus16_demux_3 (.bus(V1_inst), .E(FU_D__V[3]), .id(LDB_B__INST));
  bus16_demux bus16_demux_4 (.bus(V2_inst), .E(and_153_out), .id(LDB_B__INST));
  not not_32 (MB_free, MB_busy);
  and and_161 (ALU_A_CLR, clr, ALU_A_CMP);
  and and_162 (ALU_B_CLR, clr, ALU_B_CMP);
  RS_FF rs_ff_20 (.S(ALU_A_LD), .C(C_ct), .R(and_159_out), .Q(ALU_A_V));  // open: nQ
  RS_FF rs_ff_21 (.S(ALU_B_LD), .C(C_ct), .R(and_160_out), .Q(ALU_B_V));  // open: nQ
  not not_33 (not_33_out, E_t);
  and and_163 (and_163_out, byte_I0_iv[0], byte_I0_iv[1], byte_I0_iv[2], byte_I0_iv[3], byte_I0[4], byte_I0[5], byte_I0[6], byte_I0_iv[7]);
  and and_164 (and_164_out, byte_I0[0], byte_I0_iv[1], byte_I0_iv[2], byte_I0_iv[3], byte_I0[4], byte_I0[5], byte_I0[6], byte_I0_iv[7]);
  and and_165 (and_165_out, byte_I0[0], byte_I0[1], byte_I0_iv[2], byte_I0_iv[3], byte_I0[4], byte_I0[5], byte_I0[6], byte_I0_iv[7]);
  res_station_debug res_station_debug_1 (
    .C(C_ct), .res(not_33_out), .E(issue), .D({byte_I0, byte_I1, byte_I2, byte_I3}), .BTB_PK(BTB_pack__iss),
    .ep_I(epoch_IS), .inst(inst_IS), .URA(CT_ISS__URA), .URB(CT_ISS__URB), .RA(CT_ISS__RA), .RB(CT_ISS__RB),
    .USC(CT_ISS__UMM), .UFL(CT_ISS__UFL), .UFU(CT_ISS__UFU), .ORC(CT_ISS__ORC), .RC(CT_ISS__RC),
    .OSC(CT_ISS__OSC), .OFL(CT_ISS__OFL), .BLOCK(CT_BLOCK), .com1(com1), .com2(com2), .com1_inst(com1_inst),
    .com2_inst(com2_inst), .clr(clr), .clr_ep(clr_ep), .clr_id(clr_id), .FU_free(FU_free), .V(CT_DISP),
    .disp_32({res_station_debug_1_disp_32, byte_D1, byte_D2, byte_D3}), .BTB_DP(BTB_DP), .ep_O(epoch_DP),
    .disp(inst_DP), .full(RS_full));
  store_controller store_controller_1 (
    .C(C_ct), .in1(ALU_A_DRD), .in2(ALU_B_DRD), .in3(DIR_RD), .in4(LDB_B__RD), .in5(1'b0), .in6(1'b0),
    .in7(1'b0), .in8(1'b0), .clr({{5{1'b0}}, DIR_CLR, ALU_B_CLR, ALU_A_CLR}),
    .D1_sel(store_controller_1_d1_sel), .D2_sel(store_controller_1_d2_sel), .ST1(CT_ROB__GEN__STA),
    .ST2(CT_ROB__GEN__STB), .out1(ALU_A_STD), .out2(ALU_B_STD), .out3(DIR_ST), .out4(LDB_B__ST),
    .V({FU_D__V, DIR_V, ALU_B_VD, ALU_A_VD}));  // open: out5, out6, out7, out8
  store_controller store_controller_2 (
    .C(C_ct), .in1(ALU_A_FRD), .in2(ALU_B_FRD), .in3(1'b0), .in4(1'b0), .in5(1'b0), .in6(1'b0), .in7(1'b0),
    .in8(1'b0), .clr({{5{1'b0}}, DIR_CLR, ALU_B_CLR, ALU_A_CLR}), .D1_sel(store_controller_2_d1_sel),
    .D2_sel(store_controller_2_d2_sel), .ST1(CT_ROB__FL__STA), .ST2(CT_ROB__FL__STB), .out1(ALU_A_STF),
    .out2(ALU_B_STF), .V({FU_F__V, ALU_B_VF, ALU_A_VF}));  // open: out3, out4, out5, out6, out7, out8
  Demultiplexer #(.Selector_Bits(4)) demultiplexer_1 (
    .sel(priorityencoder_1_num), .in(and_176_out), .out_0(demultiplexer_1_out_0[0]),
    .out_1(demultiplexer_1_out_0[1]), .out_2(demultiplexer_1_out_0[2]), .out_3(demultiplexer_1_out_0[3]),
    .out_4(demultiplexer_1_out_0[4]), .out_5(demultiplexer_1_out_0[5]), .out_6(demultiplexer_1_out_0[6]),
    .out_7(demultiplexer_1_out_0[7]), .out_8(demultiplexer_1_out_0[8]), .out_9(demultiplexer_1_out_0[9]),
    .out_10(demultiplexer_1_out_0[10]), .out_11(demultiplexer_1_out_0[11]),
    .out_12(demultiplexer_1_out_0[12]), .out_13(demultiplexer_1_out_0[13]),
    .out_14(demultiplexer_1_out_0[14]), .out_15(demultiplexer_1_out_0[15]));
  Demultiplexer #(.Selector_Bits(4)) demultiplexer_2 (
    .sel(CT_FU__INST), .in(CT_RET__LD), .out_0(demultiplexer_2_out_0[0]), .out_1(demultiplexer_2_out_0[1]),
    .out_2(demultiplexer_2_out_0[2]), .out_3(demultiplexer_2_out_0[3]), .out_4(demultiplexer_2_out_0[4]),
    .out_5(demultiplexer_2_out_0[5]), .out_6(demultiplexer_2_out_0[6]), .out_7(demultiplexer_2_out_0[7]),
    .out_8(demultiplexer_2_out_0[8]), .out_9(demultiplexer_2_out_0[9]), .out_10(demultiplexer_2_out_0[10]),
    .out_11(demultiplexer_2_out_0[11]), .out_12(demultiplexer_2_out_0[12]),
    .out_13(demultiplexer_2_out_0[13]), .out_14(demultiplexer_2_out_0[14]), .out_15(demultiplexer_2_out_0[15]));
  or or_57 (or_57_out, JPU_INT, JPU_RET);
  nor nor_8 (nor_8_out, JPU_INT, JPU_RET);
  nor nor_9 (nor_9_out, JPU_INT, JPU_RET);
  assign CT_BLOCK = and_165_out ? 1'b1 : 1'bz;  // Driver driver_157
  assign issue = and_165_out ? issue_e : 1'bz;  // Driver driver_158
  assign CT_ISS__HALT = and_165_out ? 1'b1 : 1'bz;  // Driver driver_159
  PullDown #(.Bits(3)) pulldown_18 (.out(CT_ISS__UFU));
  PullDown pulldown_19 (.out(CT_ISS__OSTB));
  PullDown pulldown_20 (.out(clr));
  PullDown pulldown_21 (.out(clr_ep));
  PullDown #(.Bits(4)) pulldown_22 (.out(clr_id));
  Multiplexer #(.Bits(32)) multiplexer_62 (.sel(JPU_INT), .in_0(CT_RF__DR), .in_1(int_vec_t), .out(multiplexer_62_out));
  BitExtender #(.inputBits(1)) bitextender_7 (.in(nor_8_out), .out(bitextender_7_out));
  BitExtender #(.inputBits(1), .outputBits(37)) bitextender_8 (.in(nor_9_out), .out(bitextender_8_out));
  BitExtender #(.inputBits(1)) bitextender_9 (.in(CT_FU__EPOCH), .out(bitextender_9_out));
  assign not_34_out = ~demultiplexer_2_out_0;  // Not not_34, 16 bits wide
  BitExtender #(.inputBits(1)) bitextender_10 (.in(CT_FU__EPOCH), .out(bitextender_10_out));
  assign issue = and_163_out ? issue_e : 1'bz;  // Driver driver_160
  assign CT_ISS__URA = and_163_out ? 1'b1 : 1'bz;  // Driver driver_161
  assign CT_ISS__RA = and_163_out ? byte_I1[7:3] : 5'bz;  // Driver driver_162
  assign CT_ISS__URB = and_163_out ? 1'b1 : 1'bz;  // Driver driver_163
  assign CT_ISS__RB = and_163_out ? 5'b11110 : 5'bz;  // Driver driver_164
  assign CT_ISS__OSC = and_163_out ? 1'b1 : 1'bz;  // Driver driver_165
  assign CT_ISS__UMM = and_163_out ? 1'b1 : 1'bz;  // Driver driver_166
  assign CT_ISS__UFU = and_163_out ? 3'b110 : 3'bz;  // Driver driver_167
  assign CT_ISS__OSTB = and_163_out ? issue_e : 1'bz;  // Driver driver_168
  assign CT_UBTB = and_163_out ? issue_e : 1'bz;  // Driver driver_169
  assign issue = and_164_out ? issue_e : 1'bz;  // Driver driver_170
  assign CT_ISS__URB = and_164_out ? 1'b1 : 1'bz;  // Driver driver_171
  assign CT_ISS__RB = and_164_out ? 5'b11110 : 5'bz;  // Driver driver_172
  assign CT_ISS__OSC = and_164_out ? 1'b1 : 1'bz;  // Driver driver_173
  assign CT_ISS__UMM = and_164_out ? 1'b1 : 1'bz;  // Driver driver_174
  assign CT_ISS__UFU = and_164_out ? 3'b110 : 3'bz;  // Driver driver_175
  assign CT_ISS__OLDB = and_164_out ? issue_e : 1'bz;  // Driver driver_176
  assign CT_UBTB = and_164_out ? issue_e : 1'bz;  // Driver driver_177
  Multiplexer #(.Bits(8)) multiplexer_63 (
    .sel(CT_DISP), .in_0(8'h72), .in_1(res_station_debug_1_disp_32), .out(byte_D0));
  Multiplexer #(.Bits(32)) multiplexer_64 (.sel(JPU_RET), .in_0(pc_read), .in_1(pc_ret__int), .out(multiplexer_64_out));
  Multiplexer #(.Bits(4)) multiplexer_65 (.sel(JPU_RET), .in_0(CT_FU__INST), .in_1(RET_INST), .out(multiplexer_65_out));
  Multiplexer multiplexer_66 (.sel(JPU_RET), .in_0(CT_FU__EPOCH), .in_1(RET_EPOCH), .out(multiplexer_66_out));
  Multiplexer #(.Bits(32)) multiplexer_67 (
    .sel(or_57_out), .in_0(R_A), .in_1(multiplexer_62_out), .out(multiplexer_67_out));
  assign and_166_out = {byte_D2, byte_D3} & bitextender_7_out;  // And and_166, 16 bits wide
  assign and_167_out = BTB_DP & bitextender_8_out;  // And and_167, 37 bits wide
  or or_58 (or_58_out, CT_JPU__JP, JPU_INT, JPU_RET);
  or or_59 (or_59_out, CT_FU__MF, JPU_RET);
  assign not_35_out = ~demultiplexer_1_out_0;  // Not not_35, 16 bits wide
  assign or_60_out = bitextender_9_out | not_34_out;  // Or or_60, 16 bits wide
  assign and_168_out = bitextender_10_out & demultiplexer_2_out_0;  // And and_168, 16 bits wide
  and and_169 (and_169_out, ~CT_JPU__LD, JPU_BTB__ST);  // And
  assign or_61_out = register_91_q | demultiplexer_2_out_0;  // Or or_61, 16 bits wide
  assign or_62_out = register_92_q | and_168_out;  // Or or_62, 16 bits wide
  // data_select_32 data_select_32_1: pin names not known; wires that end beside it: store_controller_1_d1_sel, store_controller_1_d2_sel, ALU_A_T__R, ALU_B_T__R, DIR, LDB_B__D, {32{1'b0}}, {32{1'b0}}, {32{1'b0}}, {32{1'b0}}, ROB_GEN_DA, ROB_GEN_DB
  data_select_8 data_select_8_1 (
    .D1_sel(store_controller_2_d1_sel), .D2_sel(store_controller_2_d2_sel), .in1(ALU_A_T__F),
    .in2(ALU_B_T__F), .in3({8{1'b0}}), .in4({8{1'b0}}), .in5({8{1'b0}}), .in6({8{1'b0}}), .in7({8{1'b0}}),
    .in8({8{1'b0}}), .out1(ROB_FL_A), .out2(ROB_FL_B));
  RS_FF rs_ff_22 (.S(CT_JPU__LD), .C(C_ct), .R(and_169_out), .Q(JPU_BTB__ST), .nQ(rs_ff_22_nq));
  Register #(.Bits(32)) register_83 (.D(multiplexer_64_out), .C(C_dt), .en(JPU_LD), .Q(JPU_PC));
  Register #(.Bits(4)) register_84 (.D(multiplexer_65_out), .C(C_ct), .en(JPU_LD), .Q(Fl_JPU__INST));
  Register register_85 (.D(multiplexer_66_out), .C(C_ct), .en(JPU_LD), .Q(Fl_JPU__EP));
  Register #(.Bits(32)) register_86 (.D(multiplexer_67_out), .C(C_dt), .en(JPU_LD), .Q(register_86_q));
  Register #(.Bits(16)) register_87 (.D(and_166_out), .C(C_dt), .en(JPU_LD), .Q(register_87_q));
  Register #(.Bits(37)) register_88 (
    .D(and_167_out), .C(C_ct), .en(JPU_LD),
    .Q({JPU_BTB__tar, JPU_BTB__pred, JPU_BTB__J, JPU_BTB__V, JPU_BTBPK[0]}));
  Register register_89 (.D(or_58_out), .C(C_ct), .en(JPU_LD), .Q(JPU_JP));
  Register register_90 (.D(or_59_out), .C(C_ct), .en(JPU_LD), .Q(JPU_MF));
  assign and_170_out = icmks_16 & not_35_out & or_61_out;  // And and_170, 16 bits wide
  or or_63 (or_63_out, CT_RET__LD, and_176_out, ext_en);
  assign and_171_out = or_60_out & or_62_out;  // And and_171, 16 bits wide
  or or_64 (or_64_out, rs_ff_22_nq, JPU_BTB__ST);
  D_FF #(.Bits(32)) d_ff_18 (.D(register_86_q), .C(C_ct), .Q(d_ff_18_q));  // open: nQ
  D_FF #(.Bits(16)) d_ff_19 (.D(register_87_q), .C(C_ct), .Q(d_ff_19_q));  // open: nQ
  and and_172 (JPU_LD, CT_JPU__LD, or_64_out);
  Register #(.Bits(16)) register_91 (.D(and_170_out), .C(C_ct), .en(or_63_out), .Q(register_91_q));
  Register #(.Bits(16)) register_92 (.D(and_171_out), .C(C_ct), .en(or_63_out), .Q(register_92_q));
  add_s16c32 add_s16c32_2 (.a(multiplexer_68_out), .b(multiplexer_69_out), .s(JPU_ADDR));  // open: c
  Multiplexer #(.Bits(32)) multiplexer_68 (.sel(JPU_JP), .in_0(JPU_PC), .in_1(d_ff_18_q), .out(multiplexer_68_out));
  Multiplexer #(.Bits(16)) multiplexer_69 (.sel(JPU_JP), .in_0(16'h4), .in_1(d_ff_19_q), .out(multiplexer_69_out));
  assign and_173_out = V1_inst & register_91_q;  // And and_173, 16 bits wide
  BitSelector #(.Selector_Bits(4)) bitselector_1 (
    .in(register_92_q), .sel(priorityencoder_1_num), .out(bitselector_1_out));
  PullDown pulldown_23 (.out(CT_ALU__M));
  PullDown pulldown_24 (.out(CT_ALU__LD));
  PullDown pulldown_25 (.out(CT_ALU__WD));
  PullDown pulldown_26 (.out(CT_ALU__WF));
  PullDown pulldown_27 (.out(CT_FU__EPOCH));
  PullDown #(.Bits(4)) pulldown_28 (.out(CT_FU__INST));
  PullDown #(.Bits(8)) pulldown_29 (.out(CT_FU__WR));
  PullDown pulldown_30 (.out(CT_DIR__LD));
  PullDown pulldown_31 (.out(CT_DIR__M));
  PullDown pulldown_32 (.out(CT_DIR__MS));
  PullDown pulldown_33 (.out(MB_ep));
  PullDown #(.Bits(4)) pulldown_34 (.out(LD_id));
  PullDown #(.Bits(32)) pulldown_35 (.out(LD_addr));
  PullDown pulldown_36 (.out(CT_STB__LD));
  PullDown pulldown_37 (.out(CT_LDB__LD));
  PullDown pulldown_38 (.out(CT_MB__LD));
  PullDown pulldown_39 (.out(CT_MB__ST));
  PullDown pulldown_40 (.out(CT_ISS__OLDB));
  PullDown pulldown_41 (.out(CT_UBTB));
  PullDown pulldown_42 (.out(CT_USCB));
  and and_174 (and_174_out, ~JPU_MF, JPU_BTB__ST);  // And
  data_select_8 data_select_8_2 (
    .D1_sel(store_controller_1_d1_sel), .D2_sel(store_controller_1_d2_sel), .in1({ALU_A_WR, ALU_A_RM}),
    .in2({ALU_B_WR, ALU_B_RM}), .in3(DIR_WR), .in4(LDB_B__WR), .in5({8{1'b0}}), .in6({8{1'b0}}),
    .in7({8{1'b0}}), .in8({8{1'b0}}), .out1(ROB_GEN_WA), .out2(ROB_GEN_WB));
  data_select_4 data_select_4_1 (
    .D1_sel(store_controller_2_d1_sel), .D2_sel(store_controller_2_d2_sel), .in1(ALU_A_INST),
    .in2(ALU_B_INST), .in3(4'b0000), .in4(4'b0000), .in5(4'b0000), .in6(4'b0000), .in7(4'b0000),
    .in8(4'b0000), .out1(ROB_FL_INSTA), .out2(ROB_FL_INSTB));
  PriorityEncoder #(.Selector_Bits(4)) priorityencoder_1 (
    .in0(and_173_out[0]), .in1(and_173_out[1]), .in2(and_173_out[2]), .in3(and_173_out[3]),
    .in4(and_173_out[4]), .in5(and_173_out[5]), .in6(and_173_out[6]), .in7(and_173_out[7]),
    .in8(and_173_out[8]), .in9(and_173_out[9]), .in10(and_173_out[10]), .in11(and_173_out[11]),
    .in12(and_173_out[12]), .in13(and_173_out[13]), .in14(and_173_out[14]), .in15(and_173_out[15]),
    .num(priorityencoder_1_num), .any(priorityencoder_1_any));
  PullDown pulldown_43 (.out(CT_RF__SCSRE));
  PullDown pulldown_44 (.out(CT_RF__SCSE));
  PullDown pulldown_45 (.out(CT_RF__SCSS));
  PullDown pulldown_46 (.out(CT_BLOCK));
  and and_175 (JPU_MFE, JPU_MF, JPU_BTB__ST);
  bus16_demux bus16_demux_5 (.bus(V1_inst), .E(and_174_out), .id(Fl_JPU__INST));
  bus16_demux bus16_demux_6 (.bus(V2_inst), .E(JPU_BTB__ST), .id(Fl_JPU__INST));
  not not_36 (not_36_out, BTB_override);
  and and_176 (and_176_out, FU_D__V[3], priorityencoder_1_any);
  xor xor_8 (JPU_MISS, JPU_BTB__J, JPU_JP);
  not not_37 (not_37_out, JPU_BTB__pred[0]);
  PullDown pulldown_47 (.out(kernel_inst));
  PullDown pulldown_48 (.out(CT_RF__E));
  PullDown pulldown_49 (.out(CT_RF__DM));
  PullDown #(.Bits(5)) pulldown_50 (.out(CT_RF__WS));
  PullDown #(.Bits(3)) pulldown_51 (.out(CT_RF__WM));
  PullDown #(.Bits(5)) pulldown_52 (.out(CT_RF__RA));
  PullDown #(.Bits(3)) pulldown_53 (.out(CT_RF__MA));
  PullDown #(.Bits(5)) pulldown_54 (.out(CT_RF__RB));
  PullDown #(.Bits(3)) pulldown_55 (.out(CT_RF__MB));
  PullDown pulldown_56 (.out(CT_RF__PCSE));
  PullDown pulldown_57 (.out(CT_RF__PCJ));
  PullDown pulldown_58 (.out(CT_RF__PCR));
  PullDown #(.Bits(3)) pulldown_59 (.out(CT_RF__SCN));
  PullDown pulldown_60 (.out(CT_RF__SCD));
  PullDown #(.Bits(9)) pulldown_61 (.out(CT_ALU__CT));
  PullDown pulldown_62 (.out(CT_ALU__M));
  PullDown pulldown_63 (.out(CT_ALU__M2));
  PullDown pulldown_64 (.out(CT_BUS__IAR));
  PullDown pulldown_65 (.out(CT_BUS__IAG));
  PullDown pulldown_66 (.out(CT_BUS__IDR));
  PullDown pulldown_67 (.out(CT_BUS__IDM));
  PullDown pulldown_68 (.out(CT_BUS__DAR));
  PullDown pulldown_69 (.out(CT_BUS__DAM));
  PullDown pulldown_70 (.out(CT_BUS__DAG));
  PullDown pulldown_71 (.out(CT_BUS__DDR));
  PullDown pulldown_72 (.out(CT_BUS__DDG));
  PullDown pulldown_73 (.out(I_LD));
  PullDown pulldown_74 (.out(D_LD));
  PullDown pulldown_75 (.out(D_ST));
  PullDown #(.Bits(2)) pulldown_76 (.out(D_MD));
  PullDown pulldown_77 (.out(CT_MVR));
  and and_177 (and_177_out, JPU_BTB__pred[0], JPU_BTB__pred[1]);
  and and_178 (and_178_out, JPU_BTB__pred[0], JPU_JP);
  and and_179 (and_179_out, JPU_BTB__pred[1], JPU_JP);
  and and_180 (and_180_out, not_37_out, not_36_out, JPU_BTB__pred[1]);
  and and_181 (and_181_out, not_37_out, not_36_out, JPU_JP);
  and and_182 (and_182_out, JPU_BTB__pred[1], not_36_out, JPU_JP);
  D_FF #(.Bits(4)) d_ff_20 (.D(priorityencoder_1_num), .C(C_ct), .Q(RET_INST));  // open: nQ
  D_FF d_ff_21 (.D(bitselector_1_out), .C(C_ct), .Q(RET_EPOCH));  // open: nQ
  and and_183 (and_183_out, ~and_187_out, and_176_out);  // And
  inst_comp inst_comp_11 (.A_id(RET_INST), .A_ep(RET_EPOCH), .B_id(clr_id), .B_ep(clr_ep), .A_old(inst_comp_11_a_old));
  and and_184 (and_184_out, ~and_187_out, and_176_out);  // And
  inst_comp inst_comp_12 (
    .A_id(priorityencoder_1_num), .A_ep(bitselector_1_out), .B_id(clr_id), .B_ep(clr_ep),
    .A_old(inst_comp_12_a_old));
  PullDown pulldown_78 (.out(CT_HALT__LD));
  // data_select_4 data_select_4_2: pin names not known; wires that end beside it: store_controller_1_d1_sel, store_controller_1_d2_sel, ALU_A_INST, ALU_B_INST, DIR_INST, LDB_B__INST, 4'b0000, 4'b0000, 4'b0000, 4'b0000, ROB_GEN_INSTA, ROB_GEN_INSTB
  and and_185 (and_185_out[6], MB_free, JPU_free);
  or or_65 (JPU_pred[1], and_177_out, and_178_out, and_179_out, BTB_override);
  or or_66 (JPU_pred[0], and_180_out, and_181_out, and_182_out);
  not not_38 (JPU_free, and_183_out);
  and and_186 (and_186_out, inst_comp_11_a_old, clr);
  D_FF d_ff_22 (.D(and_184_out), .C(C_ct), .Q(d_ff_22_q));  // open: nQ
  and and_187 (and_187_out, inst_comp_12_a_old, clr);
  PullDown pulldown_79 (.out(issue));
  PullDown pulldown_80 (.out(CT_ISS__URA));
  PullDown pulldown_81 (.out(CT_ISS__URB));
  PullDown #(.Bits(5)) pulldown_82 (.out(CT_ISS__RA));
  PullDown #(.Bits(5)) pulldown_83 (.out(CT_ISS__RB));
  PullDown pulldown_84 (.out(CT_ISS__UMM));
  PullDown pulldown_85 (.out(CT_ISS__UFL));
  PullDown pulldown_86 (.out(CT_ISS__ORC));
  PullDown #(.Bits(5)) pulldown_87 (.out(CT_ISS__RC));
  PullDown pulldown_88 (.out(CT_ISS__OSC));
  PullDown pulldown_89 (.out(CT_ISS__OFL));
  PullDown pulldown_90 (.out(CT_ROB__EX__E));
  PullDown pulldown_91 (.out(CT_ROB__ST__E));
  PullDown #(.Bits(3)) pulldown_92 (.out(CT_SP__MOF));
  PullDown pulldown_93 (.out(CT_BUS__DDM));
  PullDown pulldown_94 (.out(CT_RF__PCH));
  PullDown pulldown_95 (.out(hlt));
  PullDown pulldown_96 (.out(ex_nop));
  PullDown pulldown_97 (.out(CT_ISS__HALT));
  Comparator #(.Bits(32)) comparator_20 (.a(JPU_ADDR), .b(JPU_BTB__tar), .eq(comparator_20_eq));  // open: gt, lt
  and and_188 (and_188_out, ~and_186_out, d_ff_22_q);  // And
  D_FF #(.Bits(8)) d_ff_23 (
    .D({JPU_free, and_185_out[6], 2'b00, MB_free, DIR_free, ALU_free, 1'b1}), .C(C_ct), .Q(FU_free));  // open: nQ
  nand nand_12 (nand_12_out, JPU_BTB__V, comparator_20_eq);
  and and_189 (and_189_out, JPU_MISS, JPU_BTB__V, comparator_20_eq);
  and and_190 (Fl_JPU, or_67_out, JPU_BTB__ST);
  assign CT_JPU__LD = and_188_out ? 1'b1 : 1'bz;  // Driver driver_178
  assign JPU_RET = and_188_out ? 1'b1 : 1'bz;  // Driver driver_179
  and and_191 (BTB_override, JPU_JP, nand_12_out);
  and and_192 (and_192_out, nand_12_out, JPU_BTB__J);
  or or_67 (or_67_out, and_189_out, and_192_out, BTB_override);
  assign CT_RF__PCSE = Fl_JPU ? 1'b1 : 1'bz;  // Driver driver_180
  assign CT_RF__PCJ = Fl_JPU ? 1'b1 : 1'bz;  // Driver driver_181
  PullDown pulldown_98 (.out(CT_JPU__JP));
  PullDown pulldown_99 (.out(JPU_A__ST));
  PullDown pulldown_100 (.out(CT_MB__OFFM));
  PullDown pulldown_101 (.out(JPU_BTB__ST));
  PullDown pulldown_102 (.out(CT_JPU__LD));
  PullDown pulldown_103 (.out(CT_FU__MF));
  PullDown pulldown_104 (.out(CT_CALL__LD));
  PullDown pulldown_105 (.out(CT_RET__LD));
  PullDown pulldown_106 (.out(JPU_RET));
  PullDown pulldown_107 (.out(JPU_free));
  PullDown pulldown_108 (.out(JPU_CALL));
  PullDown pulldown_109 (.out(CT_CALLM));

  assign CLK_str = 1'b0;
  assign CSH_mode = 2'b00;
  assign CSH_run = 1'b0;
  assign DMA_sel = 3'b000;
  assign DMA_str = 1'b0;
  assign INT_str = 1'b0;
  assign MMU_sel = 2'b00;
  assign MMU_str = 1'b0;

  // Other names for the same wires on the sheet: disp_32[31:0] = {byte_D0, byte_D1, byte_D2, byte_D3};
  //   imm16_2[15:0] = {byte_D2, byte_D3}; FU_CLR[2:0] = {DIR_CLR, ALU_B_CLR, ALU_A_CLR}; ALU_A_WR[2:0] = ALU_A_RM;
  //   ALU_B_WR[2:0] = ALU_B_RM; BTB_packet[2] = BTB_JP; BTB_pred[1:0] = BTB_packet[4:3];
  //   BTB_tar[31:0] = BTB_packet[36:5]; BTB_V = BTB_packet[1]; C_i = C_dt; Fl_INT__EP = com2_ep;
  //   Fl_INT__INST[3:0] = com2_inst; CT_RF__SCAS = CT_RF__SCAE; fl_i[8] = FL[14]; int_proc = FL[14]; trap = FL[15];
  //   FU_D__V[2:0] = {DIR_V, ALU_B_VD, ALU_A_VD}; LDB_B__V = FU_D__V[3]; FU_F__V[1:0] = {ALU_B_VF, ALU_A_VF};
  //   issue_32[31:0] = {byte_I0, byte_I1, byte_I2, byte_I3};
  //   JPU_BTBPK[36:1] = {JPU_BTB__tar, JPU_BTB__pred, JPU_BTB__J, JPU_BTB__V}; JPU_EN = JPU_BTB__ST;
  //   JPU_ST = JPU_BTB__ST; Fl_INT = INT_out; run_int = INT_out; scs_i[31:0] = ISC_i

  // Notes on the sheet:
  //   D_MD: 0:32
  //   1:16
  //   2:8
  //   3:u.u
  //   I_valid: default 1
  //   D_accept: default 1
  //   C: Hz: 4096
  //   tests
  //   IO pins
  //   primeary signals
  //   pipeline controller
  //   halt
  //   kernal mode system
  //   interrupt system
  //   inst id manager
  //   contents of rom_1 (hex, n*v repeats v):
  //   39,a,10000
  //   decode circuit
  //   ALU
  //   register
  //   stack
  //   RAM
  //   register system
  //   ROB
  //   program counter controller
  //   bus system
  //   data bus ctrl
  //   jump
  //   call
  //   return
  //   block
  //   stack circuit
  //   ALU system
  //   dir circuit
  //   load/store circuit
  //   issue circuit
  //   flag circuit
  //   FU aribiter
  //   jmp circuit
  //   return unit
  //   control bus
endmodule
